// Logisim project ALU.circ as structural Verilog: 1 circuit, main circuit main
module main (
  input  MSB,
  input  in_2,
  input  in_3,
  input  in_4,
  input  in_5,
  input  in_6,
  input  in_7,
  input  LSB,
  input  Clear,
  input  Read,
  input  in_11,
  input  Add,
  input  Subtract,
  input  Multiply,
  input  Divide,
  input  Modulo,
  input  And,
  input  Not_A,
  input  Not_B,
  input  Compare,
  input  in_21,
  input  in_22,
  output out_23,
  output A_B,
  output A_B_2,
  output A_B_3
);

  wire and_1_out, and_2_out, and_3_out, and_4_out, and_5_out, and_6_out, and_7_out, and_8_out, and_9_out,
       and_10_out, and_11_out, and_12_out, and_13_out, and_14_out, and_15_out, and_16_out, and_17_out,
       and_18_out, and_19_out, and_20_out, and_21_out, and_22_out, and_23_out, and_24_out, and_33_out,
       and_34_out, and_35_out, and_36_out, and_37_out, and_38_out, and_39_out, and_40_out, and_41_out,
       and_42_out, and_43_out, and_44_out, and_45_out, and_46_out, and_47_out, and_48_out, and_49_out,
       and_50_out, and_51_out, and_52_out, and_53_out, and_54_out, and_55_out, and_56_out, and_57_out,
       and_58_out, and_59_out, and_60_out, and_61_out, and_62_out, and_63_out, and_64_out, and_65_out,
       and_66_out, and_67_out, and_68_out, and_69_out, and_70_out, and_71_out, and_72_out, and_73_out,
       and_74_out, and_75_out, and_76_out, and_77_out, and_78_out, and_79_out, and_80_out, and_81_out,
       and_82_out, and_83_out, and_84_out, and_85_out, and_86_out, and_87_out, and_88_out, and_89_out,
       and_90_out, and_91_out, and_92_out, and_93_out, and_94_out, and_95_out, and_96_out, and_97_out,
       and_98_out, and_99_out, and_100_out, and_101_out, and_102_out, and_103_out, and_104_out, and_105_out,
       and_106_out, and_107_out, and_108_out, and_109_out, and_110_out, and_111_out, and_112_out,
       and_113_out, and_114_out, and_115_out, and_116_out, and_117_out, and_118_out, and_119_out,
       and_120_out, and_121_out, and_122_out, and_123_out, and_124_out, and_125_out, and_126_out,
       and_127_out, and_129_out, and_130_out, and_131_out, and_132_out, and_133_out, and_134_out,
       and_135_out, and_136_out, and_137_out, and_138_out, and_139_out, and_140_out, and_141_out,
       and_142_out, and_143_out, and_144_out, and_145_out, and_146_out, and_147_out, and_148_out,
       and_149_out, and_150_out, and_151_out, and_152_out, and_153_out, and_154_out, and_155_out,
       and_158_out, clock_1_out, d_ff_1_q, d_ff_2_q, d_ff_3_q, d_ff_4_q, d_ff_5_q, d_ff_6_q, d_ff_7_q,
       d_ff_8_q, nand_1_out, nand_2_out, nand_3_out, nand_4_out, nand_5_out, nand_6_out, nand_7_out,
       nand_8_out, nand_9_out, nand_10_out, nand_11_out, nand_12_out, nand_13_out, nand_14_out, nand_15_out,
       nand_16_out, nand_17_out, nand_18_out, nand_19_out, nand_20_out, nand_21_out, nand_22_out,
       nand_23_out, nand_24_out, nor_1_out, nor_2_out, nor_3_out, nor_4_out, not_1_out, not_2_out, not_3_out,
       not_4_out, not_5_out, not_6_out, not_7_out, not_8_out, not_9_out, not_10_out, not_11_out, not_12_out,
       not_13_out, not_14_out, not_15_out, not_16_out, not_17_out, not_18_out, not_19_out, not_20_out,
       not_21_out, not_22_out, not_23_out, not_24_out, not_25_out, not_26_out, not_27_out, not_28_out,
       or_1_out, or_2_out, or_3_out, or_4_out, or_5_out, or_6_out, or_7_out, or_8_out, or_9_out, or_10_out,
       or_11_out, or_12_out, or_13_out, or_16_out, or_17_out, or_18_out, or_19_out, or_20_out, or_21_out,
       or_22_out, or_23_out, or_24_out, xor_1_out, xor_2_out, xor_3_out, xor_4_out, xor_5_out, xor_6_out,
       xor_7_out, xor_8_out, xor_9_out, xor_10_out, xor_11_out, xor_12_out, xor_13_out, xor_14_out,
       xor_15_out, xor_16_out, xor_17_out, xor_18_out, xor_19_out, xor_20_out, xor_21_out, xor_22_out,
       xor_23_out, xor_24_out, xor_25_out, xor_26_out, xor_27_out, xor_28_out, xor_29_out, xor_30_out,
       xor_31_out, xor_32_out, xor_33_out, xor_34_out, xor_35_out, xor_36_out, xor_37_out, xor_38_out,
       xor_39_out, xor_40_out, xor_41_out;

  and and_1 (and_1_out, Add, LSB);
  and and_2 (and_2_out, Add, in_7);
  and and_3 (and_3_out, Add, in_6);
  and and_4 (and_4_out, Add, in_5);
  and and_5 (and_5_out, Add, in_4);
  and and_6 (and_6_out, Add, in_3);
  and and_7 (and_7_out, Add, in_2);
  and and_8 (and_8_out, Add, MSB);
  and and_9 (and_9_out, LSB, Subtract);
  and and_10 (and_10_out, in_7, Subtract);
  and and_11 (and_11_out, in_6, Subtract);
  and and_12 (and_12_out, in_5, Subtract);
  and and_13 (and_13_out, in_4, Subtract);
  and and_14 (and_14_out, in_3, Subtract);
  and and_15 (and_15_out, in_2, Subtract);
  and and_16 (and_16_out, MSB, Subtract);
  and and_17 (and_17_out, Multiply, LSB);
  and and_18 (and_18_out, Multiply, in_7);
  and and_19 (and_19_out, Multiply, in_6);
  and and_20 (and_20_out, Multiply, in_5);
  and and_21 (and_21_out, Multiply, in_4);
  and and_22 (and_22_out, Multiply, in_3);
  and and_23 (and_23_out, Multiply, in_2);
  and and_24 (and_24_out, Multiply, MSB);
  // AND_Gate and_25 has open pins: in0=Divide, in1=LSB, out=open
  // AND_Gate and_26 has open pins: in0=Divide, in1=in_7, out=open
  // AND_Gate and_27 has open pins: in0=Divide, in1=in_6, out=open
  // AND_Gate and_28 has open pins: in0=Divide, in1=in_5, out=open
  // AND_Gate and_29 has open pins: in0=Divide, in1=in_4, out=open
  // AND_Gate and_30 has open pins: in0=Divide, in1=in_3, out=open
  // AND_Gate and_31 has open pins: in0=Divide, in1=in_2, out=open
  // AND_Gate and_32 has open pins: in0=Divide, in1=MSB, out=open
  not not_1 (not_1_out, and_9_out);
  not not_2 (not_2_out, and_10_out);
  not not_3 (not_3_out, and_11_out);
  not not_4 (not_4_out, and_12_out);
  xor xor_1 (xor_1_out, and_1_out, and_5_out);
  and and_33 (and_33_out, and_5_out, and_1_out);
  xor xor_2 (xor_2_out, and_2_out, and_6_out);
  and and_34 (and_34_out, and_2_out, and_6_out);
  xor xor_3 (xor_3_out, and_3_out, and_7_out);
  and and_35 (and_35_out, and_3_out, and_7_out);
  xor xor_4 (xor_4_out, and_4_out, and_8_out);
  and and_36 (and_36_out, and_4_out, and_8_out);
  xor xor_5 (xor_5_out, not_1_out, and_13_out);
  and and_37 (and_37_out, not_1_out, and_13_out);
  xor xor_6 (xor_6_out, not_2_out, and_14_out);
  and and_38 (and_38_out, not_2_out, and_14_out);
  xor xor_7 (xor_7_out, not_3_out, and_15_out);
  and and_39 (and_39_out, not_3_out, and_15_out);
  xor xor_8 (xor_8_out, not_4_out, and_16_out);
  and and_40 (and_40_out, not_4_out, and_16_out);
  xor xor_9 (xor_9_out, xor_2_out, and_33_out);
  and and_41 (and_41_out, and_33_out, xor_2_out);
  xor xor_10 (xor_10_out, xor_3_out, or_1_out);
  and and_42 (and_42_out, or_1_out, xor_3_out);
  xor xor_11 (xor_11_out, xor_4_out, or_2_out);
  and and_43 (and_43_out, or_2_out, xor_4_out);
  xor xor_12 (xor_12_out, xor_5_out, in_21);
  and and_44 (and_44_out, in_21, xor_5_out);
  xor xor_13 (xor_13_out, xor_6_out, or_4_out);
  and and_45 (and_45_out, or_4_out, xor_6_out);
  xor xor_14 (xor_14_out, xor_7_out, or_5_out);
  and and_46 (and_46_out, or_5_out, xor_7_out);
  xor xor_15 (xor_15_out, xor_8_out, or_6_out);
  and and_47 (and_47_out, or_6_out, xor_8_out);
  and and_48 (and_48_out, and_21_out, and_17_out);
  and and_49 (and_49_out, and_21_out, and_18_out);
  and and_50 (and_50_out, and_21_out, and_19_out);
  and and_51 (and_51_out, and_21_out, and_20_out);
  and and_52 (and_52_out, and_22_out, and_17_out);
  and and_53 (and_53_out, and_22_out, and_18_out);
  and and_54 (and_54_out, and_22_out, and_19_out);
  and and_55 (and_55_out, and_22_out, and_20_out);
  and and_56 (and_56_out, and_23_out, and_17_out);
  and and_57 (and_57_out, and_23_out, and_18_out);
  and and_58 (and_58_out, and_23_out, and_19_out);
  and and_59 (and_59_out, and_23_out, and_20_out);
  and and_60 (and_60_out, and_24_out, and_17_out);
  and and_61 (and_61_out, and_24_out, and_18_out);
  and and_62 (and_62_out, and_24_out, and_19_out);
  and and_63 (and_63_out, and_24_out, and_20_out);
  or or_1 (or_1_out, and_41_out, and_34_out);
  or or_2 (or_2_out, and_42_out, and_35_out);
  or or_3 (or_3_out, and_43_out, and_36_out);
  or or_4 (or_4_out, and_44_out, and_37_out);
  or or_5 (or_5_out, and_45_out, and_38_out);
  or or_6 (or_6_out, and_46_out, and_39_out);
  or or_7 (or_7_out, and_47_out, and_40_out);
  xor xor_16 (xor_16_out, or_6_out, or_7_out);
  and and_64 (and_64_out, Not_A, LSB);
  and and_65 (and_65_out, Not_A, in_7);
  and and_66 (and_66_out, Not_A, in_6);
  and and_67 (and_67_out, Not_A, in_5);
  and and_68 (and_68_out, Not_A, in_4);
  and and_69 (and_69_out, in_3, Not_A);
  and and_70 (and_70_out, in_2, Not_A);
  and and_71 (and_71_out, MSB, Not_A);
  and and_72 (and_72_out, And, LSB);
  and and_73 (and_73_out, And, in_7);
  and and_74 (and_74_out, And, in_6);
  and and_75 (and_75_out, And, in_5);
  and and_76 (and_76_out, Not_B, in_4);
  and and_77 (and_77_out, Not_B, in_3);
  and and_78 (and_78_out, Not_B, in_2);
  and and_79 (and_79_out, Not_B, MSB);
  and and_80 (and_80_out, Compare, LSB);
  and and_81 (and_81_out, Compare, in_7);
  and and_82 (and_82_out, Compare, in_6);
  and and_83 (and_83_out, Compare, in_5);
  and and_84 (and_84_out, Compare, in_4);
  and and_85 (and_85_out, Compare, in_3);
  and and_86 (and_86_out, Compare, in_2);
  and and_87 (and_87_out, Compare, MSB);
  and and_88 (and_88_out, and_49_out, and_52_out);
  xor xor_17 (xor_17_out, and_53_out, and_50_out);
  and and_89 (and_89_out, and_53_out, and_50_out);
  xor xor_18 (xor_18_out, and_54_out, and_51_out);
  and and_90 (and_90_out, and_54_out, and_51_out);
  xor xor_19 (xor_19_out, and_55_out, in_22);
  and and_91 (and_91_out, and_55_out, in_22);
  and and_92 (and_92_out, and_61_out, and_58_out);
  xor xor_20 (xor_20_out, and_62_out, and_59_out);
  and and_93 (and_93_out, and_62_out, and_59_out);
  and and_94 (and_94_out, and_63_out, in_22);
  not not_5 (not_5_out, and_72_out);
  not not_6 (not_6_out, and_73_out);
  not not_7 (not_7_out, and_74_out);
  not not_8 (not_8_out, and_75_out);
  not not_9 (not_9_out, and_76_out);
  not not_10 (not_10_out, and_77_out);
  not not_11 (not_11_out, and_78_out);
  not not_12 (not_12_out, and_79_out);
  xor xor_21 (xor_21_out, and_52_out, and_49_out);
  xor xor_22 (xor_22_out, xor_18_out, or_9_out);
  and and_95 (and_95_out, or_9_out, xor_18_out);
  xor xor_23 (xor_23_out, and_60_out, and_57_out);
  and and_96 (and_96_out, and_57_out, and_60_out);
  xor xor_24 (xor_24_out, and_61_out, and_58_out);
  and and_97 (and_97_out, or_11_out, xor_20_out);
  xor xor_25 (xor_25_out, and_63_out, in_22);
  and and_98 (and_98_out, and_64_out, and_68_out);
  and and_99 (and_99_out, and_65_out, and_69_out);
  and and_100 (and_100_out, and_66_out, and_70_out);
  and and_101 (and_101_out, and_67_out, and_71_out);
  xor xor_26 (xor_26_out, xor_17_out, and_88_out);
  and and_102 (and_102_out, and_88_out, xor_17_out);
  or or_8 (or_8_out, and_95_out, and_90_out);
  xor xor_27 (xor_27_out, xor_19_out, or_8_out);
  and and_103 (and_103_out, or_8_out, xor_19_out);
  xor xor_28 (xor_28_out, xor_24_out, and_96_out);
  and and_104 (and_104_out, and_96_out, xor_24_out);
  xor xor_29 (xor_29_out, xor_20_out, or_11_out);
  xor xor_30 (xor_30_out, xor_25_out, or_12_out);
  and and_105 (and_105_out, or_12_out, xor_25_out);
  not not_13 (not_13_out, and_83_out);
  not not_14 (not_14_out, and_87_out);
  not not_15 (not_15_out, and_82_out);
  not not_16 (not_16_out, and_86_out);
  not not_17 (not_17_out, and_81_out);
  not not_18 (not_18_out, and_85_out);
  not not_19 (not_19_out, and_80_out);
  not not_20 (not_20_out, and_84_out);
  or or_9 (or_9_out, and_102_out, and_89_out);
  or or_10 (or_10_out, and_103_out, and_91_out);
  or or_11 (or_11_out, and_104_out, and_92_out);
  or or_12 (or_12_out, and_97_out, and_93_out);
  or or_13 (or_13_out, and_105_out, and_94_out);
  and and_106 (and_106_out, not_5_out, And);
  and and_107 (and_107_out, not_6_out, And);
  and and_108 (and_108_out, not_7_out, And);
  and and_109 (and_109_out, not_8_out, And);
  and and_110 (and_110_out, not_9_out, Not_B);
  and and_111 (and_111_out, not_10_out, Not_B);
  and and_112 (and_112_out, not_11_out, Not_B);
  and and_113 (and_113_out, not_12_out, Not_B);
  and and_114 (and_114_out, not_13_out, and_87_out);
  and and_115 (and_115_out, and_83_out, not_14_out);
  and and_116 (and_116_out, not_15_out, and_86_out);
  and and_117 (and_117_out, and_82_out, not_16_out);
  and and_118 (and_118_out, not_17_out, and_85_out);
  and and_119 (and_119_out, and_81_out, not_18_out);
  and and_120 (and_120_out, not_19_out, and_84_out);
  and and_121 (and_121_out, and_80_out, not_20_out);
  nor nor_1 (nor_1_out, and_114_out, and_115_out);
  nor nor_2 (nor_2_out, and_116_out, and_117_out);
  nor nor_3 (nor_3_out, and_118_out, and_119_out);
  nor nor_4 (nor_4_out, and_120_out, and_121_out);
  and and_122 (and_122_out, nor_1_out, and_116_out);
  and and_123 (and_123_out, nor_1_out, and_117_out);
  and and_124 (and_124_out, nor_1_out, nor_2_out, and_118_out);
  and and_125 (and_125_out, nor_1_out, nor_2_out, and_119_out);
  and and_126 (and_126_out, nor_1_out, nor_2_out, nor_3_out, and_120_out);
  and and_127 (and_127_out, nor_1_out, nor_2_out, nor_3_out, and_121_out);
  and and_128 (A_B_3, nor_1_out, nor_2_out, nor_3_out, nor_4_out);
  or or_14 (A_B, and_114_out, and_124_out, and_126_out, and_122_out);
  or or_15 (A_B_2, and_115_out, and_123_out, and_125_out, and_127_out);
  xor xor_31 (xor_31_out, xor_26_out, and_56_out);
  and and_129 (and_129_out, and_56_out, xor_26_out);
  xor xor_32 (xor_32_out, xor_22_out, xor_23_out);
  and and_130 (and_130_out, xor_22_out, xor_23_out);
  xor xor_33 (xor_33_out, xor_27_out, xor_28_out);
  and and_131 (and_131_out, xor_27_out, xor_28_out);
  xor xor_34 (xor_34_out, or_10_out, xor_29_out);
  and and_132 (and_132_out, or_10_out, xor_29_out);
  xor xor_35 (xor_35_out, in_22, xor_30_out);
  and and_133 (and_133_out, in_22, xor_30_out);
  xor xor_36 (xor_36_out, in_22, or_13_out);
  and and_134 (and_134_out, in_22, or_13_out);
  xor xor_37 (xor_37_out, xor_32_out, and_129_out);
  and and_135 (and_135_out, and_129_out, xor_32_out);
  xor xor_38 (xor_38_out, xor_33_out, or_16_out);
  and and_136 (and_136_out, or_16_out, xor_33_out);
  xor xor_39 (xor_39_out, xor_34_out, or_17_out);
  and and_137 (and_137_out, or_17_out, xor_34_out);
  xor xor_40 (xor_40_out, xor_35_out, or_18_out);
  and and_138 (and_138_out, or_18_out, xor_35_out);
  xor xor_41 (xor_41_out, xor_36_out, or_19_out);
  and and_139 (and_139_out, or_19_out, xor_36_out);
  or or_16 (or_16_out, and_135_out, and_130_out);
  or or_17 (or_17_out, and_136_out, and_131_out);
  or or_18 (or_18_out, and_137_out, and_132_out);
  or or_19 (or_19_out, and_138_out, and_133_out);
  or or_20 (or_20_out, and_139_out, and_134_out);
  or or_21 (or_21_out, and_48_out, and_98_out, xor_1_out, and_106_out, and_110_out);
  or or_22 (or_22_out, xor_21_out, and_99_out, xor_9_out, and_107_out, and_108_out);
  or or_23 (or_23_out, xor_31_out, and_100_out, xor_10_out, and_111_out, and_112_out);
  or or_24 (or_24_out, xor_37_out, and_101_out, xor_11_out, and_109_out, and_113_out);
  or or_25 (out_23, or_3_out, xor_16_out, or_20_out);
  and and_140 (and_140_out, Read, in_11);
  and and_141 (and_141_out, in_11, Clear);
  not not_21 (not_21_out, and_141_out);
  and and_142 (and_142_out, Read, in_11);
  not not_22 (not_22_out, and_143_out);
  and and_143 (and_143_out, in_11, Clear);
  and and_144 (and_144_out, Read, in_11);
  and and_145 (and_145_out, in_11, Clear);
  not not_23 (not_23_out, and_145_out);
  and and_146 (and_146_out, Read, in_11);
  and and_147 (and_147_out, in_11, Clear);
  not not_24 (not_24_out, and_147_out);
  and and_148 (and_148_out, Read, Multiply);
  not not_25 (not_25_out, and_149_out);
  and and_149 (and_149_out, Multiply, Clear);
  and and_150 (and_150_out, Read, Multiply);
  not not_26 (not_26_out, and_151_out);
  and and_151 (and_151_out, Multiply, Clear);
  and and_152 (and_152_out, Read, Multiply);
  not not_27 (not_27_out, and_153_out);
  and and_153 (and_153_out, Multiply, Clear);
  and and_154 (and_154_out, Read, Multiply);
  not not_28 (not_28_out, and_155_out);
  and and_155 (and_155_out, Multiply, Clear);
  nand nand_1 (nand_1_out, not_21_out, or_21_out);
  nand nand_2 (nand_2_out, not_21_out, d_ff_1_q);
  nand nand_3 (nand_3_out, not_22_out, or_22_out);
  nand nand_4 (nand_4_out, not_22_out, d_ff_2_q);
  nand nand_5 (nand_5_out, not_23_out, or_23_out);
  nand nand_6 (nand_6_out, not_23_out, d_ff_3_q);
  nand nand_7 (nand_7_out, not_24_out, or_24_out);
  nand nand_8 (nand_8_out, not_24_out, d_ff_4_q);
  nand nand_9 (nand_9_out, not_25_out, xor_38_out);
  nand nand_10 (nand_10_out, not_25_out, d_ff_5_q);
  nand nand_11 (nand_11_out, not_26_out, xor_39_out);
  nand nand_12 (nand_12_out, not_26_out, d_ff_6_q);
  nand nand_13 (nand_13_out, not_27_out, xor_40_out);
  nand nand_14 (nand_14_out, not_27_out, d_ff_7_q);
  nand nand_15 (nand_15_out, not_28_out, xor_41_out);
  nand nand_16 (nand_16_out, not_28_out, d_ff_8_q);
  Clock clock_1 (.out(clock_1_out));
  nand nand_17 (nand_17_out, nand_1_out, nand_2_out);
  nand nand_18 (nand_18_out, nand_3_out, nand_4_out);
  nand nand_19 (nand_19_out, nand_5_out, nand_6_out);
  nand nand_20 (nand_20_out, nand_7_out, nand_8_out);
  nand nand_21 (nand_21_out, nand_9_out, nand_10_out);
  nand nand_22 (nand_22_out, nand_11_out, nand_12_out);
  nand nand_23 (nand_23_out, nand_13_out, nand_14_out);
  nand nand_24 (nand_24_out, nand_15_out, nand_16_out);
  D_Flip_Flop d_ff_1 (.clk(clock_1_out), .D(nand_17_out), .Q(d_ff_1_q));  // open: Qn, preset, en, reset
  // AND_Gate and_156 has open pins: in0=and_140_out, in1=d_ff_1_q, out=open
  D_Flip_Flop d_ff_2 (.clk(clock_1_out), .D(nand_18_out), .Q(d_ff_2_q));  // open: Qn, preset, en, reset
  // AND_Gate and_157 has open pins: in0=and_142_out, in1=d_ff_2_q, out=open
  D_Flip_Flop d_ff_3 (.clk(clock_1_out), .D(nand_19_out), .Q(d_ff_3_q));  // open: Qn, preset, en, reset
  and and_158 (and_158_out, and_144_out, d_ff_3_q);
  D_Flip_Flop d_ff_4 (.clk(clock_1_out), .D(nand_20_out), .Q(d_ff_4_q));  // open: Qn, preset, en, reset
  // AND_Gate and_159 has open pins: in0=and_146_out, in1=d_ff_4_q, out=open
  // AND_Gate and_160 has open pins: in0=and_148_out, in1=d_ff_5_q, out=open
  D_Flip_Flop d_ff_5 (.clk(clock_1_out), .D(nand_21_out), .Q(d_ff_5_q));  // open: Qn, preset, en, reset
  D_Flip_Flop d_ff_6 (.clk(clock_1_out), .D(nand_22_out), .Q(d_ff_6_q));  // open: Qn, preset, en, reset
  // AND_Gate and_161 has open pins: in0=and_150_out, in1=d_ff_6_q, out=open
  D_Flip_Flop d_ff_7 (.clk(clock_1_out), .D(nand_23_out), .Q(d_ff_7_q));  // open: Qn, preset, en, reset
  // AND_Gate and_162 has open pins: in0=and_152_out, in1=d_ff_7_q, out=open
  D_Flip_Flop d_ff_8 (.clk(clock_1_out), .D(nand_24_out), .Q(d_ff_8_q));  // open: Qn, preset, en, reset
  // AND_Gate and_163 has open pins: in0=and_154_out, in1=d_ff_8_q, out=open

  // Notes on the sheet:
  //   Modula
  //   ALU
  //   1
  //   2
  //   Accumulator Register
  //   ERROR
endmodule
