// Logisim project Control Unit.circ as structural Verilog: 5 circuits, main circuit main
module main (
  input  in_1,
  input  in_2,
  input  in_3,
  input  MSB,
  input  in_5,
  input  in_6,
  input  in_7,
  input  in_8,
  input  in_9,
  input  in_10,
  input  LSB,
  input  Clear_Counter,
  input  Enable_Counter,
  input  Clear,
  input  Read,
  input  in_16,
  input  in_17,
  input  in_18,
  input  in_19,
  input  in_20,
  input  in_21,
  input  Address_Line,
  input  in_23,
  input  in_24,
  input  in_25,
  input  in_26,
  input  And,
  input  in_28,
  input  in_29,
  input  in_30,
  input  Not_B,
  input  in_32,
  input  in_33,
  input  in_34,
  input  in_35,
  input  LSB_2,
  input  in_37,
  input  in_38,
  input  in_39,
  input  ALU_output,
  input  in_41,
  input  in_42,
  input  MSB_2,
  input  ERROR,
  input  A_B,
  input  A_B_2,
  input  A_B_3,
  input  in_48,
  input  in_49,
  input  in_50,
  input  in_51,
  input  in_52,
  input  in_53,
  input  in_54,
  input  Read_2,
  input  in_56,
  input  Clear_2,
  input  Read_3,
  input  in_59,
  input  in_60,
  input  Input,
  input  Clear_3,
  input  Read_4,
  input  in_64,
  input  in_65,
  input  in_66,
  input  Address,
  input  _0_7,
  input  in_69,
  output out_70,
  output LSB_3,
  output out_72,
  output out_73,
  output Counter_Enable,
  output MSB_3,
  output Counter_Clear,
  output LSB_4,
  output out_78,
  output out_79,
  output MSB_4,
  output Do_NOTHING,
  output out_82,
  output out_83,
  output out_84,
  output out_85,
  output Read_5,
  output out_87,
  output out_88,
  output out_89,
  output out_90,
  output out_91,
  output out_92,
  output out_93,
  output out_94,
  output out_95,
  output LSB_5,
  output out_97,
  output out_98,
  output out_99,
  output out_100,
  output out_101,
  output MSB_5,
  output out_103,
  output out_104,
  output out_105,
  output out_106,
  output out_107,
  output out_108,
  output out_109,
  output A_B_4,
  output A_B_5,
  output A_B_6
);

  wire and_1_out, and_2_out, and_3_out, and_4_out, and_5_out, and_6_out, and_7_out, and_8_out, and_9_out,
       and_10_out, and_11_out, and_12_out, and_13_out, and_14_out, and_15_out, and_16_out, and_17_out,
       and_18_out, and_19_out, and_20_out, and_21_out, and_22_out, and_23_out, and_24_out, and_25_out,
       and_26_out, and_27_out, and_28_out, and_29_out, and_30_out, and_31_out, and_32_out, and_33_out,
       and_34_out, and_35_out, and_36_out, and_37_out, and_38_out, and_41_out, and_42_out, and_43_out,
       and_44_out, and_45_out, and_46_out, and_47_out, and_48_out, and_49_out, and_50_out, and_51_out,
       and_52_out, and_53_out, and_54_out, and_55_out, and_56_out, and_57_out, and_58_out, and_59_out,
       and_60_out, and_61_out, and_62_out, and_63_out, and_64_out, and_65_out, and_66_out, and_67_out,
       and_68_out, and_69_out, and_70_out, and_71_out, and_72_out, and_73_out, and_74_out, and_75_out,
       and_76_out, and_77_out, and_78_out, and_79_out, and_80_out, and_81_out, and_82_out, and_83_out,
       and_84_out, and_85_out, and_86_out, and_87_out, and_88_out, and_89_out, and_90_out, and_91_out,
       and_92_out, and_93_out, and_94_out, and_95_out, and_96_out, and_97_out, and_98_out, and_99_out,
       and_100_out, and_101_out, and_102_out, and_103_out, and_105_out, and_106_out, and_107_out,
       and_108_out, and_109_out, and_110_out, and_111_out, and_112_out, and_113_out, and_114_out,
       and_115_out, and_116_out, and_117_out, and_118_out, and_119_out, and_120_out, and_121_out,
       and_122_out, and_123_out, and_124_out, and_125_out, and_126_out, and_127_out, and_128_out,
       and_129_out, and_130_out, and_131_out, and_132_out, and_133_out, and_134_out, and_135_out,
       and_136_out, and_137_out, and_138_out, and_139_out, and_140_out, and_141_out, and_142_out,
       and_143_out, and_144_out, and_145_out, and_146_out, and_147_out, and_148_out, and_149_out,
       and_150_out, and_151_out, and_152_out, and_153_out, and_154_out, and_155_out, and_156_out,
       and_157_out, and_158_out, and_159_out, and_160_out, and_161_out, and_162_out, and_164_out,
       and_165_out, and_167_out, and_171_out, and_172_out, and_173_out, and_174_out, and_175_out,
       and_176_out, and_183_out, and_184_out, and_185_out, and_186_out, and_197_out, and_198_out,
       and_199_out, and_200_out, and_201_out, and_202_out, and_203_out, and_204_out, and_205_out,
       and_206_out, and_207_out, and_208_out, and_209_out, and_210_out, and_211_out, and_212_out,
       and_225_out, and_226_out, and_227_out, and_228_out, and_229_out, and_230_out, and_231_out,
       and_232_out, and_241_out, and_242_out, and_243_out, and_244_out, and_245_out, and_246_out,
       and_247_out, and_248_out, and_249_out, and_250_out, and_251_out, and_252_out, and_253_out,
       and_254_out, and_255_out, and_256_out, and_257_out, and_258_out, and_259_out, and_260_out,
       and_261_out, and_262_out, and_263_out, and_264_out, and_265_out, and_266_out, and_267_out,
       and_268_out, and_269_out, and_270_out, and_271_out, and_272_out, and_273_out, and_274_out,
       and_275_out, and_276_out, and_277_out, and_278_out, and_279_out, and_280_out, and_281_out,
       and_282_out, and_283_out, and_284_out, and_285_out, and_286_out, and_287_out, and_288_out,
       and_289_out, and_290_out, and_291_out, and_292_out, and_293_out, and_294_out, and_295_out,
       and_296_out, and_297_out, and_298_out, and_299_out, and_300_out, and_301_out, and_302_out,
       and_303_out, and_304_out, and_305_out, and_306_out, and_307_out, and_308_out, and_309_out,
       and_310_out, and_311_out, and_312_out, and_313_out, and_314_out, and_315_out, and_316_out,
       and_317_out, and_318_out, and_319_out, and_320_out, and_321_out, and_322_out, and_323_out,
       and_324_out, and_325_out, and_326_out, and_327_out, and_328_out, and_329_out, and_330_out,
       and_331_out, and_332_out, and_333_out, and_334_out, and_335_out, and_336_out, and_337_out,
       and_338_out, and_339_out, and_340_out, and_341_out, and_342_out, and_343_out, and_344_out,
       and_345_out, and_346_out, and_347_out, and_348_out, and_349_out, and_350_out, and_351_out,
       and_352_out, and_353_out, and_354_out, and_355_out, and_357_out, and_358_out, and_359_out,
       and_360_out, and_361_out, and_362_out, and_363_out, and_364_out, and_365_out, and_366_out,
       and_367_out, and_368_out, and_369_out, and_370_out, and_371_out, and_372_out, and_373_out,
       and_374_out, and_375_out, and_376_out, and_377_out, and_378_out, and_379_out, and_380_out,
       and_381_out, and_382_out, and_383_out, clock_1_out, clock_2_out, clock_3_out, clock_4_out,
       clock_5_out, d_ff_1_q, d_ff_2_q, d_ff_3_q, d_ff_4_q, d_ff_5_q, d_ff_6_q, d_ff_7_q, d_ff_8_q, d_ff_9_q,
       d_ff_10_q, d_ff_11_q, d_ff_12_q, d_ff_13_q, d_ff_14_q, d_ff_15_q, d_ff_16_q, d_ff_17_q, d_ff_18_q,
       d_ff_19_q, d_ff_20_q, d_ff_21_q, d_ff_22_q, d_ff_23_q, d_ff_24_q, d_ff_25_q, d_ff_26_q, d_ff_27_q,
       d_ff_28_q, d_ff_29_q, d_ff_30_q, d_ff_31_q, d_ff_32_q, d_ff_33_q, d_ff_34_q, d_ff_35_q, d_ff_36_q,
       d_ff_37_q, d_ff_38_q, d_ff_39_q, d_ff_40_q, d_ff_41_q, d_ff_42_q, d_ff_43_q, d_ff_44_q, d_ff_45_q,
       d_ff_46_q, d_ff_47_q, d_ff_48_q, d_ff_49_q, d_ff_50_q, d_ff_51_q, d_ff_52_q, d_ff_53_q, d_ff_54_q,
       d_ff_55_q, d_ff_56_q, j_k_ff_7_q, j_k_ff_8_q, nand_1_out, nand_2_out, nand_3_out, nand_4_out,
       nand_5_out, nand_6_out, nand_7_out, nand_8_out, nand_9_out, nand_10_out, nand_11_out, nand_12_out,
       nand_13_out, nand_14_out, nand_15_out, nand_16_out, nand_17_out, nand_18_out, nand_19_out,
       nand_20_out, nand_21_out, nand_22_out, nand_23_out, nand_24_out, nand_25_out, nand_26_out,
       nand_27_out, nand_28_out, nand_29_out, nand_30_out, nand_31_out, nand_32_out, nand_33_out,
       nand_34_out, nand_35_out, nand_36_out, nand_37_out, nand_38_out, nand_39_out, nand_40_out,
       nand_41_out, nand_42_out, nand_43_out, nand_44_out, nand_45_out, nand_46_out, nand_47_out,
       nand_48_out, nand_49_out, nand_50_out, nand_51_out, nand_52_out, nand_53_out, nand_54_out,
       nand_55_out, nand_56_out, nand_57_out, nand_58_out, nand_59_out, nand_60_out, nand_61_out,
       nand_62_out, nand_63_out, nand_64_out, nand_65_out, nand_66_out, nand_67_out, nand_68_out,
       nand_69_out, nand_70_out, nand_71_out, nand_72_out, nand_73_out, nand_74_out, nand_75_out,
       nand_76_out, nand_77_out, nand_78_out, nand_79_out, nand_80_out, nand_81_out, nand_82_out,
       nand_83_out, nand_84_out, nand_85_out, nand_86_out, nand_87_out, nand_88_out, nand_89_out,
       nand_90_out, nand_91_out, nand_92_out, nand_93_out, nand_94_out, nand_95_out, nand_96_out,
       nand_97_out, nand_98_out, nand_99_out, nand_100_out, nand_101_out, nand_102_out, nand_103_out,
       nand_104_out, nand_105_out, nand_106_out, nand_107_out, nand_108_out, nand_109_out, nand_110_out,
       nand_111_out, nand_112_out, nand_113_out, nand_114_out, nand_115_out, nand_116_out, nand_117_out,
       nand_118_out, nand_119_out, nand_120_out, nand_121_out, nand_122_out, nand_123_out, nand_124_out,
       nand_125_out, nand_126_out, nand_127_out, nand_128_out, nand_129_out, nand_130_out, nand_131_out,
       nand_132_out, nand_133_out, nand_134_out, nand_135_out, nand_136_out, nand_137_out, nand_138_out,
       nand_139_out, nand_140_out, nand_141_out, nand_142_out, nand_143_out, nand_144_out, nand_145_out,
       nand_146_out, nand_147_out, nand_148_out, nand_149_out, nand_150_out, nand_151_out, nand_152_out,
       nand_153_out, nand_154_out, nand_155_out, nand_156_out, nand_157_out, nand_158_out, nand_159_out,
       nand_160_out, nand_161_out, nand_162_out, nand_163_out, nand_164_out, nand_165_out, nand_166_out,
       nand_167_out, nand_168_out, nor_1_out, nor_2_out, nor_3_out, nor_4_out, not_1_out, not_2_out,
       not_3_out, not_4_out, not_5_out, not_6_out, not_7_out, not_8_out, not_9_out, not_10_out, not_11_out,
       not_12_out, not_13_out, not_14_out, not_15_out, not_16_out, not_17_out, not_18_out, not_19_out,
       not_20_out, not_21_out, not_22_out, not_23_out, not_24_out, not_25_out, not_26_out, not_27_out,
       not_28_out, not_29_out, not_30_out, not_31_out, not_32_out, not_33_out, not_34_out, not_35_out,
       not_36_out, not_37_out, not_38_out, not_39_out, not_40_out, not_41_out, not_42_out, not_43_out,
       not_44_out, not_45_out, not_46_out, not_47_out, not_48_out, not_49_out, not_50_out, not_51_out,
       not_52_out, not_53_out, not_54_out, not_55_out, not_56_out, not_57_out, not_58_out, not_59_out,
       not_60_out, not_61_out, not_62_out, not_63_out, not_64_out, not_65_out, not_66_out, not_67_out,
       not_68_out, not_69_out, not_70_out, not_71_out, not_72_out, not_73_out, not_74_out, not_75_out,
       not_76_out, not_77_out, not_78_out, not_79_out, not_80_out, not_81_out, not_82_out, not_83_out,
       not_84_out, not_85_out, not_86_out, not_87_out, or_5_out, or_6_out, or_7_out, or_8_out, or_9_out,
       or_10_out, or_11_out, or_12_out, or_13_out, or_14_out, or_15_out, or_16_out, or_17_out, or_20_out,
       or_21_out, or_22_out, or_23_out, or_24_out, or_25_out, or_26_out, or_27_out, or_28_out, undriven,
       undriven_2, undriven_3, undriven_4, undriven_5, xor_1_out, xor_2_out, xor_3_out, xor_4_out, xor_5_out,
       xor_6_out, xor_7_out, xor_8_out, xor_9_out, xor_10_out, xor_11_out, xor_12_out, xor_13_out,
       xor_14_out, xor_15_out, xor_16_out, xor_17_out, xor_18_out, xor_19_out, xor_20_out, xor_21_out,
       xor_22_out, xor_23_out, xor_24_out, xor_25_out, xor_26_out, xor_27_out, xor_28_out, xor_29_out,
       xor_30_out, xor_31_out, xor_32_out, xor_33_out, xor_34_out, xor_35_out, xor_36_out, xor_37_out,
       xor_38_out, xor_39_out, xor_40_out, xor_41_out;

  and and_1 (and_1_out, in_2, in_3);
  and and_2 (and_2_out, in_3, in_1);
  and and_3 (and_3_out, in_2, in_3);
  and and_4 (and_4_out, in_3, in_1);
  and and_5 (and_5_out, in_2, in_3);
  and and_6 (and_6_out, in_3, in_1);
  and and_7 (and_7_out, in_2, in_3);
  and and_8 (and_8_out, in_3, in_1);
  and and_9 (and_9_out, in_2, in_3);
  and and_10 (and_10_out, in_3, in_1);
  and and_11 (and_11_out, in_2, in_3);
  and and_12 (and_12_out, in_3, in_1);
  and and_13 (and_13_out, in_2, in_3);
  and and_14 (and_14_out, in_3, in_1);
  and and_15 (and_15_out, in_2, in_3);
  and and_16 (and_16_out, in_3, in_1);
  not not_1 (not_1_out, in_66);
  not not_2 (not_2_out, Address);
  not not_3 (not_3_out, _0_7);
  not not_4 (not_4_out, and_2_out);
  not not_5 (not_5_out, and_4_out);
  not not_6 (not_6_out, and_6_out);
  not not_7 (not_7_out, and_8_out);
  not not_8 (not_8_out, and_10_out);
  not not_9 (not_9_out, and_12_out);
  not not_10 (not_10_out, and_14_out);
  not not_11 (not_11_out, and_16_out);
  nand nand_1 (nand_1_out, not_4_out, and_153_out);
  nand nand_2 (nand_2_out, not_4_out, d_ff_1_q);
  nand nand_3 (nand_3_out, not_5_out, and_154_out);
  nand nand_4 (nand_4_out, not_5_out, d_ff_2_q);
  nand nand_5 (nand_5_out, not_6_out, and_155_out);
  nand nand_6 (nand_6_out, not_6_out, d_ff_3_q);
  nand nand_7 (nand_7_out, not_7_out, and_156_out);
  nand nand_8 (nand_8_out, not_7_out, d_ff_4_q);
  nand nand_9 (nand_9_out, not_8_out, and_157_out);
  nand nand_10 (nand_10_out, not_8_out, d_ff_5_q);
  nand nand_11 (nand_11_out, not_9_out, and_158_out);
  nand nand_12 (nand_12_out, not_9_out, d_ff_6_q);
  not nand_13 (nand_13_out, not_10_out);  // NAND_Gate
  nand nand_14 (nand_14_out, not_10_out, d_ff_7_q);
  not nand_15 (nand_15_out, not_11_out);  // NAND_Gate
  nand nand_16 (nand_16_out, not_11_out, d_ff_8_q);
  and and_17 (and_17_out, in_66, Address);
  and and_18 (and_18_out, Address, not_3_out);
  and and_19 (and_19_out, _0_7, not_2_out);
  and and_20 (and_20_out, not_3_out, not_2_out);
  and and_21 (and_21_out, Address, not_1_out);
  and and_22 (and_22_out, not_1_out, not_3_out);
  and and_23 (and_23_out, not_1_out, not_2_out);
  and and_24 (and_24_out, not_1_out, not_2_out);
  Clock clock_1 (.out(clock_1_out));
  D_Flip_Flop d_ff_1 (.clk(clock_1_out), .D(nand_17_out), .Q(d_ff_1_q));  // open: Qn, preset, en, reset
  nand nand_17 (nand_17_out, nand_1_out, nand_2_out);
  D_Flip_Flop d_ff_2 (.clk(clock_1_out), .D(nand_18_out), .Q(d_ff_2_q));  // open: Qn, preset, en, reset
  nand nand_18 (nand_18_out, nand_3_out, nand_4_out);
  D_Flip_Flop d_ff_3 (.clk(clock_1_out), .D(nand_19_out), .Q(d_ff_3_q));  // open: Qn, preset, en, reset
  nand nand_19 (nand_19_out, nand_5_out, nand_6_out);
  D_Flip_Flop d_ff_4 (.clk(clock_1_out), .D(nand_20_out), .Q(d_ff_4_q));  // open: Qn, preset, en, reset
  nand nand_20 (nand_20_out, nand_7_out, nand_8_out);
  D_Flip_Flop d_ff_5 (.clk(clock_1_out), .D(nand_21_out), .Q(d_ff_5_q));  // open: Qn, preset, en, reset
  nand nand_21 (nand_21_out, nand_9_out, nand_10_out);
  D_Flip_Flop d_ff_6 (.clk(clock_1_out), .D(nand_22_out), .Q(d_ff_6_q));  // open: Qn, preset, en, reset
  nand nand_22 (nand_22_out, nand_11_out, nand_12_out);
  D_Flip_Flop d_ff_7 (.clk(clock_1_out), .D(nand_23_out), .Q(d_ff_7_q));  // open: Qn, preset, en, reset
  nand nand_23 (nand_23_out, nand_13_out, nand_14_out);
  D_Flip_Flop d_ff_8 (.clk(clock_1_out), .D(nand_24_out), .Q(d_ff_8_q));  // open: Qn, preset, en, reset
  nand nand_24 (nand_24_out, nand_15_out, nand_16_out);
  and and_25 (and_25_out, _0_7, and_17_out);
  and and_26 (and_26_out, in_66, and_18_out);
  and and_27 (and_27_out, in_66, and_19_out);
  and and_28 (and_28_out, in_66, and_20_out);
  and and_29 (and_29_out, _0_7, and_21_out);
  and and_30 (and_30_out, Address, and_22_out);
  and and_31 (and_31_out, _0_7, and_23_out);
  and and_32 (and_32_out, and_24_out, not_3_out);
  and and_33 (and_33_out, and_1_out, d_ff_1_q);
  and and_34 (and_34_out, and_3_out, d_ff_2_q);
  and and_35 (and_35_out, and_5_out, d_ff_3_q);
  and and_36 (and_36_out, and_7_out, d_ff_4_q);
  and and_37 (and_37_out, and_9_out, d_ff_5_q);
  and and_38 (and_38_out, and_11_out, d_ff_6_q);
  // AND_Gate and_39 has open pins: in0=and_13_out, in1=d_ff_7_q, out=open
  // AND_Gate and_40 has open pins: in0=and_15_out, in1=d_ff_8_q, out=open
  Clock clock_2 (.out(clock_2_out));
  J_K_Flip_Flop #(.trigger("falling")) j_k_ff_1 (
    .J(Enable_Counter), .clk(clock_2_out), .K(Enable_Counter), .Q(and_33_out), .preset(and_42_out),
    .reset(Clear_Counter));  // open: Qn, en
  and and_41 (and_41_out, Enable_Counter, and_33_out);
  and and_42 (and_42_out, in_18, in_21);
  and and_43 (and_43_out, in_18, in_23);
  and and_44 (and_44_out, in_18, in_26);
  and and_45 (and_45_out, in_18, in_29);
  and and_46 (and_46_out, in_18, in_32);
  and and_47 (and_47_out, in_18, in_33);
  and and_48 (and_48_out, in_18, in_35);
  and and_49 (and_49_out, in_18, in_37);
  and and_50 (and_50_out, Read_4, and_25_out);
  not not_12 (not_12_out, and_51_out);
  and and_51 (and_51_out, and_25_out, Clear_3);
  and and_52 (and_52_out, Read_4, and_25_out);
  and and_53 (and_53_out, and_25_out, Clear_3);
  not not_13 (not_13_out, and_53_out);
  and and_54 (and_54_out, Read_4, and_25_out);
  not not_14 (not_14_out, and_55_out);
  and and_55 (and_55_out, and_25_out, Clear_3);
  and and_56 (and_56_out, Read_4, and_25_out);
  and and_57 (and_57_out, and_25_out, Clear_3);
  not not_15 (not_15_out, and_57_out);
  and and_58 (and_58_out, Read_4, and_26_out);
  not not_16 (not_16_out, and_59_out);
  and and_59 (and_59_out, and_26_out, Clear_3);
  and and_60 (and_60_out, Read_4, and_26_out);
  not not_17 (not_17_out, and_61_out);
  and and_61 (and_61_out, and_26_out, Clear_3);
  and and_62 (and_62_out, Read_4, and_26_out);
  and and_63 (and_63_out, and_26_out, Clear_3);
  not not_18 (not_18_out, and_63_out);
  and and_64 (and_64_out, Read_4, and_26_out);
  and and_65 (and_65_out, and_26_out, Clear_3);
  not not_19 (not_19_out, and_65_out);
  and and_66 (and_66_out, Read_4, and_27_out);
  not not_20 (not_20_out, and_67_out);
  and and_67 (and_67_out, and_27_out, Clear_3);
  and and_68 (and_68_out, Read_4, and_27_out);
  and and_69 (and_69_out, and_27_out, Clear_3);
  not not_21 (not_21_out, and_69_out);
  and and_70 (and_70_out, Read_4, and_27_out);
  not not_22 (not_22_out, and_71_out);
  and and_71 (and_71_out, and_27_out, Clear_3);
  and and_72 (and_72_out, Read_4, and_27_out);
  not not_23 (not_23_out, and_73_out);
  and and_73 (and_73_out, and_27_out, Clear_3);
  and and_74 (and_74_out, Read_4, and_28_out);
  not not_24 (not_24_out, and_75_out);
  and and_75 (and_75_out, and_28_out, Clear_3);
  and and_76 (and_76_out, Read_4, and_28_out);
  not not_25 (not_25_out, and_77_out);
  and and_77 (and_77_out, and_28_out, Clear_3);
  and and_78 (and_78_out, Read_4, and_28_out);
  and and_79 (and_79_out, and_28_out, Clear_3);
  not not_26 (not_26_out, and_79_out);
  and and_80 (and_80_out, Read_4, and_28_out);
  and and_81 (and_81_out, and_28_out, Clear_3);
  not not_27 (not_27_out, and_81_out);
  and and_82 (and_82_out, and_41_out, and_34_out);
  nand nand_25 (nand_25_out, not_12_out, in_59);
  nand nand_26 (nand_26_out, not_12_out, d_ff_9_q);
  nand nand_27 (nand_27_out, not_13_out, Input);
  nand nand_28 (nand_28_out, not_13_out, d_ff_10_q);
  nand nand_29 (nand_29_out, not_14_out, in_64);
  nand nand_30 (nand_30_out, not_14_out, d_ff_11_q);
  nand nand_31 (nand_31_out, not_15_out, in_65);
  nand nand_32 (nand_32_out, not_15_out, d_ff_12_q);
  nand nand_33 (nand_33_out, not_16_out, in_59);
  nand nand_34 (nand_34_out, not_16_out, d_ff_13_q);
  nand nand_35 (nand_35_out, not_17_out, Input);
  nand nand_36 (nand_36_out, not_17_out, d_ff_14_q);
  nand nand_37 (nand_37_out, not_18_out, in_64);
  nand nand_38 (nand_38_out, not_18_out, d_ff_15_q);
  nand nand_39 (nand_39_out, not_19_out, in_65);
  nand nand_40 (nand_40_out, not_19_out, d_ff_16_q);
  nand nand_41 (nand_41_out, not_20_out, in_59);
  nand nand_42 (nand_42_out, not_20_out, d_ff_17_q);
  nand nand_43 (nand_43_out, not_21_out, Input);
  nand nand_44 (nand_44_out, not_21_out, d_ff_18_q);
  nand nand_45 (nand_45_out, not_22_out, in_64);
  nand nand_46 (nand_46_out, not_22_out, d_ff_19_q);
  nand nand_47 (nand_47_out, not_23_out, in_65);
  nand nand_48 (nand_48_out, not_23_out, d_ff_20_q);
  nand nand_49 (nand_49_out, not_24_out, in_59);
  nand nand_50 (nand_50_out, not_24_out, d_ff_21_q);
  nand nand_51 (nand_51_out, not_25_out, Input);
  nand nand_52 (nand_52_out, not_25_out, d_ff_22_q);
  nand nand_53 (nand_53_out, not_26_out, in_64);
  nand nand_54 (nand_54_out, not_26_out, d_ff_23_q);
  nand nand_55 (nand_55_out, not_27_out, in_65);
  nand nand_56 (nand_56_out, not_27_out, d_ff_24_q);
  J_K_Flip_Flop #(.trigger("falling")) j_k_ff_2 (
    .J(and_41_out), .clk(clock_2_out), .K(and_41_out), .Q(and_34_out), .preset(and_43_out),
    .reset(Clear_Counter));  // open: Qn, en
  and and_83 (and_83_out, and_82_out, and_35_out);
  Clock clock_3 (.out(clock_3_out));
  nand nand_57 (nand_57_out, nand_25_out, nand_26_out);
  nand nand_58 (nand_58_out, nand_27_out, nand_28_out);
  nand nand_59 (nand_59_out, nand_29_out, nand_30_out);
  nand nand_60 (nand_60_out, nand_31_out, nand_32_out);
  nand nand_61 (nand_61_out, nand_33_out, nand_34_out);
  nand nand_62 (nand_62_out, nand_35_out, nand_36_out);
  nand nand_63 (nand_63_out, nand_37_out, nand_38_out);
  nand nand_64 (nand_64_out, nand_39_out, nand_40_out);
  nand nand_65 (nand_65_out, nand_41_out, nand_42_out);
  nand nand_66 (nand_66_out, nand_43_out, nand_44_out);
  nand nand_67 (nand_67_out, nand_45_out, nand_46_out);
  nand nand_68 (nand_68_out, nand_47_out, nand_48_out);
  nand nand_69 (nand_69_out, nand_49_out, nand_50_out);
  nand nand_70 (nand_70_out, nand_51_out, nand_52_out);
  nand nand_71 (nand_71_out, nand_53_out, nand_54_out);
  nand nand_72 (nand_72_out, nand_55_out, nand_56_out);
  J_K_Flip_Flop #(.trigger("falling")) j_k_ff_3 (
    .J(and_82_out), .clk(clock_2_out), .K(and_82_out), .Q(and_35_out), .preset(and_44_out),
    .reset(Clear_Counter));  // open: Qn, en
  and and_84 (and_84_out, and_83_out, and_36_out);
  D_Flip_Flop d_ff_9 (.clk(clock_3_out), .D(nand_57_out), .Q(d_ff_9_q));  // open: Qn, preset, en, reset
  and and_85 (and_85_out, and_50_out, d_ff_9_q);
  D_Flip_Flop d_ff_10 (.clk(clock_3_out), .D(nand_58_out), .Q(d_ff_10_q));  // open: Qn, preset, en, reset
  and and_86 (and_86_out, and_52_out, d_ff_10_q);
  D_Flip_Flop d_ff_11 (.clk(clock_3_out), .D(nand_59_out), .Q(d_ff_11_q));  // open: Qn, preset, en, reset
  and and_87 (and_87_out, and_54_out, d_ff_11_q);
  D_Flip_Flop d_ff_12 (.clk(clock_3_out), .D(nand_60_out), .Q(d_ff_12_q));  // open: Qn, preset, en, reset
  and and_88 (and_88_out, and_56_out, d_ff_12_q);
  and and_89 (and_89_out, and_58_out, d_ff_13_q);
  D_Flip_Flop d_ff_13 (.clk(clock_3_out), .D(nand_61_out), .Q(d_ff_13_q));  // open: Qn, preset, en, reset
  D_Flip_Flop d_ff_14 (.clk(clock_3_out), .D(nand_62_out), .Q(d_ff_14_q));  // open: Qn, preset, en, reset
  and and_90 (and_90_out, and_60_out, d_ff_14_q);
  D_Flip_Flop d_ff_15 (.clk(clock_3_out), .D(nand_63_out), .Q(d_ff_15_q));  // open: Qn, preset, en, reset
  and and_91 (and_91_out, and_62_out, d_ff_15_q);
  D_Flip_Flop d_ff_16 (.clk(clock_3_out), .D(nand_64_out), .Q(d_ff_16_q));  // open: Qn, preset, en, reset
  and and_92 (and_92_out, and_64_out, d_ff_16_q);
  D_Flip_Flop d_ff_17 (.clk(clock_3_out), .D(nand_65_out), .Q(d_ff_17_q));  // open: Qn, preset, en, reset
  and and_93 (and_93_out, and_66_out, d_ff_17_q);
  D_Flip_Flop d_ff_18 (.clk(clock_3_out), .D(nand_66_out), .Q(d_ff_18_q));  // open: Qn, preset, en, reset
  and and_94 (and_94_out, and_68_out, d_ff_18_q);
  D_Flip_Flop d_ff_19 (.clk(clock_3_out), .D(nand_67_out), .Q(d_ff_19_q));  // open: Qn, preset, en, reset
  and and_95 (and_95_out, and_70_out, d_ff_19_q);
  D_Flip_Flop d_ff_20 (.clk(clock_3_out), .D(nand_68_out), .Q(d_ff_20_q));  // open: Qn, preset, en, reset
  and and_96 (and_96_out, and_72_out, d_ff_20_q);
  D_Flip_Flop d_ff_21 (.clk(clock_3_out), .D(nand_69_out), .Q(d_ff_21_q));  // open: Qn, preset, en, reset
  and and_97 (and_97_out, and_74_out, d_ff_21_q);
  D_Flip_Flop d_ff_22 (.clk(clock_3_out), .D(nand_70_out), .Q(d_ff_22_q));  // open: Qn, preset, en, reset
  and and_98 (and_98_out, and_76_out, d_ff_22_q);
  D_Flip_Flop d_ff_23 (.clk(clock_3_out), .D(nand_71_out), .Q(d_ff_23_q));  // open: Qn, preset, en, reset
  and and_99 (and_99_out, and_78_out, d_ff_23_q);
  D_Flip_Flop d_ff_24 (.clk(clock_3_out), .D(nand_72_out), .Q(d_ff_24_q));  // open: Qn, preset, en, reset
  and and_100 (and_100_out, and_80_out, d_ff_24_q);
  J_K_Flip_Flop #(.trigger("falling")) j_k_ff_4 (
    .J(and_83_out), .clk(clock_2_out), .K(and_83_out), .Q(and_36_out), .preset(and_45_out),
    .reset(Clear_Counter));  // open: Qn, en
  and and_101 (and_101_out, and_84_out, and_37_out);
  J_K_Flip_Flop #(.trigger("falling")) j_k_ff_5 (
    .J(and_84_out), .clk(clock_2_out), .K(and_84_out), .Q(and_37_out), .preset(and_46_out),
    .reset(Clear_Counter));  // open: Qn, en
  and and_102 (and_102_out, and_101_out, and_38_out);
  J_K_Flip_Flop #(.trigger("falling")) j_k_ff_6 (
    .J(and_101_out), .clk(clock_2_out), .K(and_101_out), .Q(and_38_out), .preset(and_47_out),
    .reset(Clear_Counter));  // open: Qn, en
  and and_103 (and_103_out, and_102_out, j_k_ff_7_q);
  J_K_Flip_Flop #(.trigger("falling")) j_k_ff_7 (
    .J(and_102_out), .clk(clock_2_out), .K(and_102_out), .Q(j_k_ff_7_q), .preset(and_48_out),
    .reset(Clear_Counter));  // open: Qn, en
  and and_104 (out_82, and_103_out, j_k_ff_8_q);
  and and_105 (and_105_out, Read_4, and_29_out);
  and and_106 (and_106_out, and_29_out, Clear_3);
  and and_107 (and_107_out, Read_4, and_29_out);
  and and_108 (and_108_out, and_29_out, Clear_3);
  and and_109 (and_109_out, Read_4, and_29_out);
  and and_110 (and_110_out, and_29_out, Clear_3);
  and and_111 (and_111_out, Read_4, and_29_out);
  and and_112 (and_112_out, and_29_out, Clear_3);
  and and_113 (and_113_out, Read_4, and_30_out);
  and and_114 (and_114_out, and_30_out, Clear_3);
  and and_115 (and_115_out, Read_4, and_30_out);
  and and_116 (and_116_out, and_30_out, Clear_3);
  and and_117 (and_117_out, Read_4, and_30_out);
  and and_118 (and_118_out, and_30_out, Clear_3);
  and and_119 (and_119_out, Read_4, and_30_out);
  and and_120 (and_120_out, and_30_out, Clear_3);
  and and_121 (and_121_out, Read_4, and_31_out);
  and and_122 (and_122_out, and_31_out, Clear_3);
  and and_123 (and_123_out, Read_4, and_31_out);
  and and_124 (and_124_out, and_31_out, Clear_3);
  and and_125 (and_125_out, Read_4, and_31_out);
  and and_126 (and_126_out, and_31_out, Clear_3);
  and and_127 (and_127_out, Read_4, and_31_out);
  and and_128 (and_128_out, and_31_out, Clear_3);
  and and_129 (and_129_out, Read_4, and_32_out);
  and and_130 (and_130_out, and_32_out, Clear_3);
  and and_131 (and_131_out, Read_4, and_32_out);
  and and_132 (and_132_out, and_32_out, Clear_3);
  and and_133 (and_133_out, Read_4, and_32_out);
  and and_134 (and_134_out, and_32_out, Clear_3);
  and and_135 (and_135_out, Read_4, and_32_out);
  and and_136 (and_136_out, and_32_out, Clear_3);
  J_K_Flip_Flop #(.trigger("falling")) j_k_ff_8 (
    .J(and_103_out), .clk(clock_2_out), .K(and_103_out), .Q(j_k_ff_8_q), .preset(and_49_out),
    .reset(Clear_Counter));  // open: Qn, en
  not not_28 (not_28_out, and_106_out);
  not not_29 (not_29_out, and_108_out);
  not not_30 (not_30_out, and_110_out);
  not not_31 (not_31_out, and_112_out);
  not not_32 (not_32_out, and_114_out);
  not not_33 (not_33_out, and_116_out);
  not not_34 (not_34_out, and_118_out);
  not not_35 (not_35_out, and_120_out);
  not not_36 (not_36_out, and_122_out);
  not not_37 (not_37_out, and_124_out);
  not not_38 (not_38_out, and_126_out);
  not not_39 (not_39_out, and_128_out);
  not not_40 (not_40_out, and_130_out);
  not not_41 (not_41_out, and_132_out);
  not not_42 (not_42_out, and_134_out);
  not not_43 (not_43_out, and_136_out);
  nand nand_73 (nand_73_out, not_28_out, in_59);
  nand nand_74 (nand_74_out, nand_73_out, nand_75_out);
  nand nand_75 (nand_75_out, not_28_out, d_ff_25_q);
  nand nand_76 (nand_76_out, not_29_out, Input);
  nand nand_77 (nand_77_out, nand_76_out, nand_78_out);
  nand nand_78 (nand_78_out, not_29_out, d_ff_26_q);
  nand nand_79 (nand_79_out, not_30_out, in_64);
  nand nand_80 (nand_80_out, nand_79_out, nand_81_out);
  nand nand_81 (nand_81_out, not_30_out, d_ff_27_q);
  nand nand_82 (nand_82_out, not_31_out, in_65);
  nand nand_83 (nand_83_out, nand_82_out, nand_84_out);
  nand nand_84 (nand_84_out, not_31_out, d_ff_28_q);
  nand nand_85 (nand_85_out, not_32_out, in_59);
  nand nand_86 (nand_86_out, nand_85_out, nand_87_out);
  nand nand_87 (nand_87_out, not_32_out, d_ff_29_q);
  nand nand_88 (nand_88_out, not_33_out, Input);
  nand nand_89 (nand_89_out, nand_88_out, nand_90_out);
  nand nand_90 (nand_90_out, not_33_out, d_ff_30_q);
  nand nand_91 (nand_91_out, not_34_out, in_64);
  nand nand_92 (nand_92_out, nand_91_out, nand_93_out);
  nand nand_93 (nand_93_out, not_34_out, d_ff_31_q);
  nand nand_94 (nand_94_out, not_35_out, in_65);
  nand nand_95 (nand_95_out, nand_94_out, nand_96_out);
  nand nand_96 (nand_96_out, not_35_out, d_ff_32_q);
  nand nand_97 (nand_97_out, not_36_out, in_59);
  nand nand_98 (nand_98_out, nand_97_out, nand_99_out);
  nand nand_99 (nand_99_out, not_36_out, d_ff_33_q);
  nand nand_100 (nand_100_out, not_37_out, Input);
  nand nand_101 (nand_101_out, nand_100_out, nand_102_out);
  nand nand_102 (nand_102_out, not_37_out, d_ff_34_q);
  nand nand_103 (nand_103_out, not_38_out, in_64);
  nand nand_104 (nand_104_out, nand_103_out, nand_105_out);
  nand nand_105 (nand_105_out, not_38_out, d_ff_35_q);
  nand nand_106 (nand_106_out, not_39_out, in_65);
  nand nand_107 (nand_107_out, nand_106_out, nand_108_out);
  nand nand_108 (nand_108_out, not_39_out, d_ff_36_q);
  nand nand_109 (nand_109_out, not_40_out, in_59);
  nand nand_110 (nand_110_out, nand_109_out, nand_111_out);
  nand nand_111 (nand_111_out, not_40_out, d_ff_37_q);
  nand nand_112 (nand_112_out, not_41_out, Input);
  nand nand_113 (nand_113_out, nand_112_out, nand_114_out);
  nand nand_114 (nand_114_out, not_41_out, d_ff_38_q);
  nand nand_115 (nand_115_out, not_42_out, in_64);
  nand nand_116 (nand_116_out, nand_115_out, nand_117_out);
  nand nand_117 (nand_117_out, not_42_out, d_ff_39_q);
  nand nand_118 (nand_118_out, not_43_out, in_65);
  nand nand_119 (nand_119_out, nand_118_out, nand_120_out);
  nand nand_120 (nand_120_out, not_43_out, d_ff_40_q);
  D_Flip_Flop d_ff_25 (.clk(clock_3_out), .D(nand_74_out), .Q(d_ff_25_q));  // open: Qn, preset, en, reset
  D_Flip_Flop d_ff_26 (.clk(clock_3_out), .D(nand_77_out), .Q(d_ff_26_q));  // open: Qn, preset, en, reset
  D_Flip_Flop d_ff_27 (.clk(clock_3_out), .D(nand_80_out), .Q(d_ff_27_q));  // open: Qn, preset, en, reset
  D_Flip_Flop d_ff_28 (.clk(clock_3_out), .D(nand_83_out), .Q(d_ff_28_q));  // open: Qn, preset, en, reset
  D_Flip_Flop d_ff_29 (.clk(clock_3_out), .D(nand_86_out), .Q(d_ff_29_q));  // open: Qn, preset, en, reset
  D_Flip_Flop d_ff_30 (.clk(clock_3_out), .D(nand_89_out), .Q(d_ff_30_q));  // open: Qn, preset, en, reset
  D_Flip_Flop d_ff_31 (.clk(clock_3_out), .D(nand_92_out), .Q(d_ff_31_q));  // open: Qn, preset, en, reset
  D_Flip_Flop d_ff_32 (.clk(clock_3_out), .D(nand_95_out), .Q(d_ff_32_q));  // open: Qn, preset, en, reset
  D_Flip_Flop d_ff_33 (.clk(clock_3_out), .D(nand_98_out), .Q(d_ff_33_q));  // open: Qn, preset, en, reset
  D_Flip_Flop d_ff_34 (.clk(clock_3_out), .D(nand_101_out), .Q(d_ff_34_q));  // open: Qn, preset, en, reset
  D_Flip_Flop d_ff_35 (.clk(clock_3_out), .D(nand_104_out), .Q(d_ff_35_q));  // open: Qn, preset, en, reset
  D_Flip_Flop d_ff_36 (.clk(clock_3_out), .D(nand_107_out), .Q(d_ff_36_q));  // open: Qn, preset, en, reset
  D_Flip_Flop d_ff_37 (.clk(clock_3_out), .D(nand_110_out), .Q(d_ff_37_q));  // open: Qn, preset, en, reset
  D_Flip_Flop d_ff_38 (.clk(clock_3_out), .D(nand_113_out), .Q(d_ff_38_q));  // open: Qn, preset, en, reset
  D_Flip_Flop d_ff_39 (.clk(clock_3_out), .D(nand_116_out), .Q(d_ff_39_q));  // open: Qn, preset, en, reset
  D_Flip_Flop d_ff_40 (.clk(clock_3_out), .D(nand_119_out), .Q(d_ff_40_q));  // open: Qn, preset, en, reset
  and and_137 (and_137_out, and_105_out, d_ff_25_q);
  and and_138 (and_138_out, and_107_out, d_ff_26_q);
  and and_139 (and_139_out, and_109_out, d_ff_27_q);
  and and_140 (and_140_out, and_111_out, d_ff_28_q);
  and and_141 (and_141_out, and_113_out, d_ff_29_q);
  and and_142 (and_142_out, and_115_out, d_ff_30_q);
  and and_143 (and_143_out, and_117_out, d_ff_31_q);
  and and_144 (and_144_out, and_119_out, d_ff_32_q);
  and and_145 (and_145_out, and_121_out, d_ff_33_q);
  and and_146 (and_146_out, and_123_out, d_ff_34_q);
  and and_147 (and_147_out, and_125_out, d_ff_35_q);
  and and_148 (and_148_out, and_127_out, d_ff_36_q);
  and and_149 (and_149_out, and_129_out, d_ff_37_q);
  and and_150 (and_150_out, and_131_out, d_ff_38_q);
  and and_151 (and_151_out, and_133_out, d_ff_39_q);
  and and_152 (and_152_out, and_135_out, d_ff_40_q);
  and and_153 (and_153_out, Read_2, and_167_out);
  and and_154 (and_154_out, in_54, and_167_out);
  and and_155 (and_155_out, in_53, and_167_out);
  and and_156 (and_156_out, in_52, and_167_out);
  and and_157 (and_157_out, Read_2, and_164_out);
  and and_158 (and_158_out, in_54, and_164_out);
  and and_159 (and_159_out, in_53, and_164_out);
  and and_160 (and_160_out, in_52, and_164_out);
  and and_161 (and_161_out, in_48, in_49, in_50, in_51);
  and and_162 (and_162_out, not_46_out, in_49, in_50, in_51);
  and and_163 (Counter_Clear, not_47_out, in_48, in_50, in_51);
  and and_164 (and_164_out, not_46_out, not_47_out, in_50, in_51);
  and and_165 (and_165_out, not_45_out, in_48, in_49, in_51);
  and and_166 (in_39, not_46_out, not_45_out, in_49, in_51);
  and and_167 (and_167_out, not_47_out, not_45_out, in_48, in_51);
  and and_168 (LSB_2, not_46_out, not_47_out, not_45_out, in_51);
  or or_1 (out_105, and_85_out, and_137_out, and_89_out, and_93_out, and_97_out, and_141_out, and_145_out, and_149_out);
  or or_2 (out_106, and_86_out, and_138_out, and_150_out, and_90_out, and_94_out, and_98_out, and_142_out, and_146_out);
  or or_3 (out_107, and_87_out, and_91_out, and_95_out, and_99_out, and_139_out, and_143_out, and_147_out, and_151_out);
  or or_4 (out_109, and_88_out, and_92_out, and_96_out, and_100_out, and_140_out, and_144_out, and_148_out, and_152_out);
  not not_44 (not_44_out, in_51);
  not not_45 (not_45_out, in_50);
  not not_46 (not_46_out, in_48);
  not not_47 (not_47_out, in_49);
  and and_169 (LSB_5, in_34, in_56);
  and and_170 (out_70, in_50, in_49, not_44_out, in_48);
  and and_171 (and_171_out, in_50, in_49, not_44_out, not_46_out);
  and and_172 (and_172_out, in_50, in_48, not_44_out, not_47_out);
  and and_173 (and_173_out, in_50, not_47_out, not_44_out, not_46_out);
  and and_174 (and_174_out, in_48, in_49, not_44_out, not_45_out);
  and and_175 (and_175_out, in_49, not_44_out, not_45_out, not_46_out);
  and and_176 (and_176_out, not_44_out, not_45_out, not_47_out, in_48);
  and and_177 (Do_NOTHING, not_44_out, not_45_out, not_47_out, not_46_out);
  and and_178 (out_97, LSB_2, in_56);
  and and_179 (out_98, in_38, in_56);
  and and_180 (out_100, ALU_output, in_56);
  and and_181 (out_99, in_39, in_56);
  and and_182 (out_101, in_41, in_56);
  and and_183 (and_183_out, and_162_out, Read_2);
  and and_184 (and_184_out, and_162_out, in_54);
  and and_185 (and_185_out, and_162_out, in_53);
  and and_186 (and_186_out, and_162_out, in_52);
  and and_187 (LSB_4, Read_2, and_161_out);
  and and_188 (out_78, in_54, and_161_out);
  and and_189 (out_79, in_53, and_161_out);
  and and_190 (MSB_4, in_52, and_161_out);
  and and_191 (MSB_5, in_42, in_56);
  and and_192 (out_103, MSB_2, in_56);
  and and_193 (and_184_out, in_39, LSB_2);
  and and_194 (and_183_out, in_39, in_34);
  and and_195 (and_186_out, in_39, in_39);
  and and_196 (and_185_out, in_39, in_38);
  and and_197 (and_197_out, Read_3, in_60);
  and and_198 (and_198_out, in_60, Clear_2);
  and and_199 (and_199_out, Read_3, in_60);
  and and_200 (and_200_out, in_60, Clear_2);
  and and_201 (and_201_out, Read_3, in_60);
  and and_202 (and_202_out, in_60, Clear_2);
  and and_203 (and_203_out, Read_3, in_60);
  and and_204 (and_204_out, in_60, Clear_2);
  and and_205 (and_205_out, Read_3, undriven_5);
  and and_206 (and_206_out, undriven_5, Clear_2);
  and and_207 (and_207_out, Read_3, undriven_5);
  and and_208 (and_208_out, undriven_5, Clear_2);
  and and_209 (and_209_out, Read_3, undriven_5);
  and and_210 (and_210_out, undriven_5, Clear_2);
  and and_211 (and_211_out, Read_3, undriven_5);
  and and_212 (and_212_out, undriven_5, Clear_2);
  not not_48 (not_48_out, and_198_out);
  not not_49 (not_49_out, and_200_out);
  not not_50 (not_50_out, and_202_out);
  not not_51 (not_51_out, and_204_out);
  not not_52 (not_52_out, and_206_out);
  not not_53 (not_53_out, and_208_out);
  not not_54 (not_54_out, and_210_out);
  not not_55 (not_55_out, and_212_out);
  not not_56 (not_56_out, and_165_out);
  not not_57 (not_57_out, and_165_out);
  not not_58 (not_58_out, and_165_out);
  not not_59 (not_59_out, and_165_out);
  nand nand_121 (nand_121_out, not_48_out, undriven_4);
  nand nand_122 (nand_122_out, not_48_out, d_ff_41_q);
  nand nand_123 (nand_123_out, not_49_out, undriven_3);
  nand nand_124 (nand_124_out, not_49_out, d_ff_42_q);
  nand nand_125 (nand_125_out, not_50_out, undriven_2);
  nand nand_126 (nand_126_out, not_50_out, d_ff_43_q);
  nand nand_127 (nand_127_out, not_51_out, undriven);
  nand nand_128 (nand_128_out, not_51_out, d_ff_44_q);
  not nand_129 (nand_129_out, not_52_out);  // NAND_Gate
  nand nand_130 (nand_130_out, not_52_out, d_ff_45_q);
  not nand_131 (nand_131_out, not_53_out);  // NAND_Gate
  nand nand_132 (nand_132_out, not_53_out, d_ff_46_q);
  not nand_133 (nand_133_out, not_54_out);  // NAND_Gate
  nand nand_134 (nand_134_out, not_54_out, d_ff_47_q);
  not nand_135 (nand_135_out, not_55_out);  // NAND_Gate
  nand nand_136 (nand_136_out, not_55_out, d_ff_48_q);
  and and_213 (LSB_3, and_183_out, not_56_out);
  and and_214 (out_72, and_184_out, not_57_out);
  and and_215 (out_73, and_185_out, not_58_out);
  and and_216 (MSB_3, and_186_out, not_59_out);
  Clock clock_4 (.out(clock_4_out));
  D_Flip_Flop d_ff_41 (.clk(clock_4_out), .D(nand_137_out), .Q(d_ff_41_q));  // open: Qn, preset, en, reset
  nand nand_137 (nand_137_out, nand_121_out, nand_122_out);
  D_Flip_Flop d_ff_42 (.clk(clock_4_out), .D(nand_138_out), .Q(d_ff_42_q));  // open: Qn, preset, en, reset
  nand nand_138 (nand_138_out, nand_123_out, nand_124_out);
  D_Flip_Flop d_ff_43 (.clk(clock_4_out), .D(nand_139_out), .Q(d_ff_43_q));  // open: Qn, preset, en, reset
  nand nand_139 (nand_139_out, nand_125_out, nand_126_out);
  D_Flip_Flop d_ff_44 (.clk(clock_4_out), .D(nand_140_out), .Q(d_ff_44_q));  // open: Qn, preset, en, reset
  nand nand_140 (nand_140_out, nand_127_out, nand_128_out);
  D_Flip_Flop d_ff_45 (.clk(clock_4_out), .D(nand_141_out), .Q(d_ff_45_q));  // open: Qn, preset, en, reset
  nand nand_141 (nand_141_out, nand_129_out, nand_130_out);
  D_Flip_Flop d_ff_46 (.clk(clock_4_out), .D(nand_142_out), .Q(d_ff_46_q));  // open: Qn, preset, en, reset
  nand nand_142 (nand_142_out, nand_131_out, nand_132_out);
  D_Flip_Flop d_ff_47 (.clk(clock_4_out), .D(nand_143_out), .Q(d_ff_47_q));  // open: Qn, preset, en, reset
  nand nand_143 (nand_143_out, nand_133_out, nand_134_out);
  D_Flip_Flop d_ff_48 (.clk(clock_4_out), .D(nand_144_out), .Q(d_ff_48_q));  // open: Qn, preset, en, reset
  nand nand_144 (nand_144_out, nand_135_out, nand_136_out);
  // AND_Gate and_217 has open pins: in0=and_197_out, in1=d_ff_41_q, out=open
  // AND_Gate and_218 has open pins: in0=and_199_out, in1=d_ff_42_q, out=open
  // AND_Gate and_219 has open pins: in0=and_201_out, in1=d_ff_43_q, out=open
  // AND_Gate and_220 has open pins: in0=and_203_out, in1=d_ff_44_q, out=open
  // AND_Gate and_221 has open pins: in0=and_205_out, in1=d_ff_45_q, out=open
  // AND_Gate and_222 has open pins: in0=and_207_out, in1=d_ff_46_q, out=open
  // AND_Gate and_223 has open pins: in0=and_209_out, in1=d_ff_47_q, out=open
  // AND_Gate and_224 has open pins: in0=and_211_out, in1=d_ff_48_q, out=open
  and and_225 (and_225_out, and_174_out, LSB);
  and and_226 (and_226_out, and_174_out, in_10);
  and and_227 (and_227_out, and_174_out, in_9);
  and and_228 (and_228_out, and_174_out, in_8);
  and and_229 (and_229_out, and_174_out, in_7);
  and and_230 (and_230_out, and_174_out, in_6);
  and and_231 (and_231_out, and_174_out, in_5);
  and and_232 (and_232_out, and_174_out, MSB);
  // AND_Gate and_233 has open pins: in0=and_173_out, in1=LSB, out=open
  // AND_Gate and_234 has open pins: in0=and_173_out, in1=in_10, out=open
  // AND_Gate and_235 has open pins: in0=and_173_out, in1=in_9, out=open
  // AND_Gate and_236 has open pins: in0=and_173_out, in1=in_8, out=open
  // AND_Gate and_237 has open pins: in0=and_173_out, in1=in_7, out=open
  // AND_Gate and_238 has open pins: in0=and_173_out, in1=in_6, out=open
  // AND_Gate and_239 has open pins: in0=and_173_out, in1=in_5, out=open
  // AND_Gate and_240 has open pins: in0=and_173_out, in1=MSB, out=open
  and and_241 (and_241_out, and_176_out, LSB);
  and and_242 (and_242_out, and_176_out, in_10);
  and and_243 (and_243_out, and_176_out, in_9);
  and and_244 (and_244_out, and_176_out, in_8);
  and and_245 (and_245_out, and_176_out, in_7);
  and and_246 (and_246_out, and_176_out, in_6);
  and and_247 (and_247_out, and_176_out, in_5);
  and and_248 (and_248_out, and_176_out, MSB);
  and and_249 (and_249_out, LSB, and_175_out);
  and and_250 (and_250_out, in_10, and_175_out);
  and and_251 (and_251_out, in_9, and_175_out);
  and and_252 (and_252_out, in_8, and_175_out);
  and and_253 (and_253_out, in_7, and_175_out);
  and and_254 (and_254_out, in_6, and_175_out);
  and and_255 (and_255_out, in_5, and_175_out);
  and and_256 (and_256_out, MSB, and_175_out);
  not not_60 (not_60_out, and_249_out);
  not not_61 (not_61_out, and_251_out);
  not not_62 (not_62_out, and_250_out);
  not not_63 (not_63_out, and_252_out);
  xor xor_1 (xor_1_out, and_241_out, and_245_out);
  and and_257 (and_257_out, and_245_out, and_241_out);
  xor xor_2 (xor_2_out, and_242_out, and_246_out);
  and and_258 (and_258_out, and_242_out, and_246_out);
  xor xor_3 (xor_3_out, and_243_out, and_247_out);
  and and_259 (and_259_out, and_243_out, and_247_out);
  xor xor_4 (xor_4_out, and_244_out, and_248_out);
  and and_260 (and_260_out, and_244_out, and_248_out);
  xor xor_5 (xor_5_out, not_60_out, and_253_out);
  and and_261 (and_261_out, not_60_out, and_253_out);
  xor xor_6 (xor_6_out, not_62_out, and_254_out);
  and and_262 (and_262_out, not_62_out, and_254_out);
  xor xor_7 (xor_7_out, not_61_out, and_255_out);
  and and_263 (and_263_out, not_61_out, and_255_out);
  xor xor_8 (xor_8_out, not_63_out, and_256_out);
  and and_264 (and_264_out, not_63_out, and_256_out);
  and and_265 (and_265_out, and_229_out, and_225_out);
  and and_266 (and_266_out, and_229_out, and_226_out);
  and and_267 (and_267_out, and_229_out, and_227_out);
  and and_268 (and_268_out, and_229_out, and_228_out);
  and and_269 (and_269_out, and_230_out, and_225_out);
  and and_270 (and_270_out, and_230_out, and_226_out);
  and and_271 (and_271_out, and_230_out, and_227_out);
  and and_272 (and_272_out, and_230_out, and_228_out);
  and and_273 (and_273_out, and_231_out, and_225_out);
  and and_274 (and_274_out, and_231_out, and_226_out);
  and and_275 (and_275_out, and_231_out, and_227_out);
  and and_276 (and_276_out, and_231_out, and_228_out);
  and and_277 (and_277_out, and_232_out, and_225_out);
  and and_278 (and_278_out, and_232_out, and_226_out);
  and and_279 (and_279_out, and_232_out, and_227_out);
  and and_280 (and_280_out, and_232_out, and_228_out);
  xor xor_9 (xor_9_out, xor_2_out, and_257_out);
  and and_281 (and_281_out, and_257_out, xor_2_out);
  xor xor_10 (xor_10_out, xor_3_out, or_5_out);
  and and_282 (and_282_out, or_5_out, xor_3_out);
  xor xor_11 (xor_11_out, xor_4_out, or_6_out);
  and and_283 (and_283_out, or_6_out, xor_4_out);
  xor xor_12 (xor_12_out, xor_5_out, and_175_out);
  and and_284 (and_284_out, and_175_out, xor_5_out);
  xor xor_13 (xor_13_out, xor_6_out, or_8_out);
  and and_285 (and_285_out, or_8_out, xor_6_out);
  xor xor_14 (xor_14_out, xor_7_out, or_9_out);
  and and_286 (and_286_out, or_9_out, xor_7_out);
  xor xor_15 (xor_15_out, xor_8_out, or_10_out);
  and and_287 (and_287_out, or_10_out, xor_8_out);
  or or_5 (or_5_out, and_281_out, and_258_out);
  or or_6 (or_6_out, and_282_out, and_259_out);
  or or_7 (or_7_out, and_283_out, and_260_out);
  or or_8 (or_8_out, and_284_out, and_261_out);
  or or_9 (or_9_out, and_285_out, and_262_out);
  or or_10 (or_10_out, and_286_out, and_263_out);
  or or_11 (or_11_out, and_287_out, and_264_out);
  and and_288 (and_288_out, xor_12_out, and_175_out);
  and and_289 (and_289_out, xor_13_out, and_175_out);
  and and_290 (and_290_out, xor_14_out, and_175_out);
  and and_291 (and_291_out, and_175_out, xor_15_out);
  xor xor_16 (xor_16_out, or_10_out, or_11_out);
  and and_292 (and_292_out, and_171_out, LSB);
  and and_293 (and_293_out, and_171_out, in_10);
  and and_294 (and_294_out, and_171_out, in_9);
  and and_295 (and_295_out, and_171_out, in_8);
  and and_296 (and_296_out, and_171_out, in_7);
  and and_297 (and_297_out, in_6, and_171_out);
  and and_298 (and_298_out, in_5, and_171_out);
  and and_299 (and_299_out, MSB, and_171_out);
  and and_300 (and_300_out, And, LSB);
  and and_301 (and_301_out, And, in_10);
  and and_302 (and_302_out, And, in_9);
  and and_303 (and_303_out, And, in_8);
  and and_304 (and_304_out, Not_B, in_7);
  and and_305 (and_305_out, Not_B, in_6);
  and and_306 (and_306_out, Not_B, in_5);
  and and_307 (and_307_out, Not_B, MSB);
  and and_308 (and_308_out, LSB_2, LSB);
  and and_309 (and_309_out, LSB_2, in_10);
  and and_310 (and_310_out, LSB_2, in_9);
  and and_311 (and_311_out, LSB_2, in_8);
  and and_312 (and_312_out, LSB_2, in_7);
  and and_313 (and_313_out, LSB_2, in_6);
  and and_314 (and_314_out, LSB_2, in_5);
  and and_315 (and_315_out, LSB_2, MSB);
  xor xor_17 (xor_17_out, and_269_out, and_266_out);
  and and_316 (and_316_out, and_266_out, and_269_out);
  xor xor_18 (xor_18_out, and_270_out, and_267_out);
  and and_317 (and_317_out, and_270_out, and_267_out);
  xor xor_19 (xor_19_out, and_271_out, and_268_out);
  and and_318 (and_318_out, and_271_out, and_268_out);
  xor xor_20 (xor_20_out, and_272_out, in_69);
  and and_319 (and_319_out, and_272_out, in_69);
  and and_320 (and_320_out, and_274_out, and_277_out);
  xor xor_21 (xor_21_out, and_278_out, and_275_out);
  and and_321 (and_321_out, and_278_out, and_275_out);
  xor xor_22 (xor_22_out, and_279_out, and_276_out);
  and and_322 (and_322_out, and_279_out, and_276_out);
  xor xor_23 (xor_23_out, and_280_out, in_69);
  and and_323 (and_323_out, and_280_out, in_69);
  and and_324 (and_324_out, and_292_out, and_296_out);
  and and_325 (and_325_out, and_293_out, and_297_out);
  and and_326 (and_326_out, and_294_out, and_298_out);
  and and_327 (and_327_out, and_295_out, and_299_out);
  not not_64 (not_64_out, and_300_out);
  not not_65 (not_65_out, and_301_out);
  not not_66 (not_66_out, and_302_out);
  not not_67 (not_67_out, and_303_out);
  not not_68 (not_68_out, and_304_out);
  not not_69 (not_69_out, and_305_out);
  not not_70 (not_70_out, and_306_out);
  not not_71 (not_71_out, and_307_out);
  and and_328 (and_328_out, and_316_out, xor_18_out);
  xor xor_24 (xor_24_out, xor_19_out, or_14_out);
  and and_329 (and_329_out, or_14_out, xor_19_out);
  and and_330 (and_330_out, or_12_out, xor_20_out);
  xor xor_25 (xor_25_out, and_277_out, and_274_out);
  xor xor_26 (xor_26_out, xor_22_out, or_16_out);
  and and_331 (and_331_out, or_16_out, xor_22_out);
  xor xor_27 (xor_27_out, xor_18_out, and_316_out);
  or or_12 (or_12_out, and_329_out, and_318_out);
  xor xor_28 (xor_28_out, xor_20_out, or_12_out);
  xor xor_29 (xor_29_out, xor_21_out, and_320_out);
  and and_332 (and_332_out, and_320_out, xor_21_out);
  or or_13 (or_13_out, and_331_out, and_322_out);
  xor xor_30 (xor_30_out, xor_23_out, or_13_out);
  and and_333 (and_333_out, or_13_out, xor_23_out);
  not not_72 (not_72_out, and_311_out);
  not not_73 (not_73_out, and_315_out);
  not not_74 (not_74_out, and_310_out);
  not not_75 (not_75_out, and_314_out);
  not not_76 (not_76_out, and_309_out);
  not not_77 (not_77_out, and_313_out);
  not not_78 (not_78_out, and_308_out);
  not not_79 (not_79_out, and_312_out);
  or or_14 (or_14_out, and_328_out, and_317_out);
  or or_15 (or_15_out, and_330_out, and_319_out);
  or or_16 (or_16_out, and_332_out, and_321_out);
  or or_17 (or_17_out, and_333_out, and_323_out);
  and and_334 (and_334_out, not_64_out, And);
  and and_335 (and_335_out, not_65_out, And);
  and and_336 (and_336_out, not_66_out, And);
  and and_337 (and_337_out, not_67_out, And);
  and and_338 (and_338_out, not_68_out, Not_B);
  and and_339 (and_339_out, not_69_out, Not_B);
  and and_340 (and_340_out, not_70_out, Not_B);
  and and_341 (and_341_out, not_71_out, Not_B);
  and and_342 (and_342_out, not_72_out, and_315_out);
  and and_343 (and_343_out, and_311_out, not_73_out);
  and and_344 (and_344_out, not_74_out, and_314_out);
  and and_345 (and_345_out, and_310_out, not_75_out);
  and and_346 (and_346_out, not_76_out, and_313_out);
  and and_347 (and_347_out, and_309_out, not_77_out);
  and and_348 (and_348_out, not_78_out, and_312_out);
  and and_349 (and_349_out, and_308_out, not_79_out);
  nor nor_1 (nor_1_out, and_342_out, and_343_out);
  nor nor_2 (nor_2_out, and_344_out, and_345_out);
  nor nor_3 (nor_3_out, and_346_out, and_347_out);
  nor nor_4 (nor_4_out, and_348_out, and_349_out);
  and and_350 (and_350_out, nor_1_out, and_344_out);
  and and_351 (and_351_out, nor_1_out, and_345_out);
  and and_352 (and_352_out, nor_1_out, nor_2_out, and_346_out);
  and and_353 (and_353_out, nor_1_out, nor_2_out, and_347_out);
  and and_354 (and_354_out, nor_1_out, nor_2_out, nor_3_out, and_348_out);
  and and_355 (and_355_out, nor_1_out, nor_2_out, nor_3_out, and_349_out);
  and and_356 (A_B_6, nor_1_out, nor_2_out, nor_3_out, nor_4_out);
  or or_18 (A_B_4, and_342_out, and_352_out, and_354_out, and_350_out);
  or or_19 (A_B_5, and_343_out, and_351_out, and_353_out, and_355_out);
  xor xor_31 (xor_31_out, xor_27_out, and_273_out);
  and and_357 (and_357_out, and_273_out, xor_27_out);
  xor xor_32 (xor_32_out, xor_24_out, xor_25_out);
  and and_358 (and_358_out, xor_24_out, xor_25_out);
  xor xor_33 (xor_33_out, xor_28_out, xor_29_out);
  and and_359 (and_359_out, xor_28_out, xor_29_out);
  xor xor_34 (xor_34_out, or_15_out, xor_26_out);
  and and_360 (and_360_out, or_15_out, xor_26_out);
  xor xor_35 (xor_35_out, in_69, xor_30_out);
  and and_361 (and_361_out, in_69, xor_30_out);
  xor xor_36 (xor_36_out, in_69, or_17_out);
  and and_362 (and_362_out, in_69, or_17_out);
  xor xor_37 (xor_37_out, xor_32_out, and_357_out);
  and and_363 (and_363_out, and_357_out, xor_32_out);
  xor xor_38 (xor_38_out, xor_33_out, or_20_out);
  and and_364 (and_364_out, or_20_out, xor_33_out);
  xor xor_39 (xor_39_out, xor_34_out, or_21_out);
  and and_365 (and_365_out, or_21_out, xor_34_out);
  xor xor_40 (xor_40_out, xor_35_out, or_22_out);
  and and_366 (and_366_out, or_22_out, xor_35_out);
  xor xor_41 (xor_41_out, xor_36_out, or_23_out);
  and and_367 (and_367_out, or_23_out, xor_36_out);
  or or_20 (or_20_out, and_363_out, and_358_out);
  or or_21 (or_21_out, and_364_out, and_359_out);
  or or_22 (or_22_out, and_365_out, and_360_out);
  or or_23 (or_23_out, and_366_out, and_361_out);
  or or_24 (or_24_out, and_367_out, and_362_out);
  or or_25 (or_25_out, and_265_out, and_324_out, xor_1_out, and_288_out, and_334_out, and_338_out);
  or or_26 (or_26_out, xor_17_out, and_325_out, xor_9_out, and_289_out, and_335_out, and_336_out);
  or or_27 (or_27_out, xor_31_out, and_326_out, xor_10_out, and_290_out, and_339_out, and_340_out);
  or or_28 (or_28_out, xor_37_out, and_327_out, xor_11_out, and_291_out, and_337_out, and_341_out);
  or or_29 (out_108, or_7_out, xor_16_out, or_24_out);
  and and_368 (and_368_out, Read, in_17);
  and and_369 (and_369_out, in_17, Clear);
  not not_80 (not_80_out, and_369_out);
  and and_370 (and_370_out, Read, in_17);
  not not_81 (not_81_out, and_371_out);
  and and_371 (and_371_out, in_17, Clear);
  and and_372 (and_372_out, Read, in_17);
  not not_82 (not_82_out, and_373_out);
  and and_373 (and_373_out, in_17, Clear);
  and and_374 (and_374_out, Read, in_17);
  and and_375 (and_375_out, in_17, Clear);
  not not_83 (not_83_out, and_375_out);
  and and_376 (and_376_out, Read, and_174_out);
  not not_84 (not_84_out, and_377_out);
  and and_377 (and_377_out, and_174_out, Clear);
  and and_378 (and_378_out, Read, and_174_out);
  not not_85 (not_85_out, and_379_out);
  and and_379 (and_379_out, and_174_out, Clear);
  and and_380 (and_380_out, Read, and_174_out);
  not not_86 (not_86_out, and_381_out);
  and and_381 (and_381_out, and_174_out, Clear);
  and and_382 (and_382_out, Read, and_174_out);
  and and_383 (and_383_out, and_174_out, Clear);
  not not_87 (not_87_out, and_383_out);
  nand nand_145 (nand_145_out, not_80_out, or_25_out);
  nand nand_146 (nand_146_out, not_80_out, d_ff_49_q);
  nand nand_147 (nand_147_out, not_81_out, or_26_out);
  nand nand_148 (nand_148_out, not_81_out, d_ff_50_q);
  nand nand_149 (nand_149_out, not_82_out, or_27_out);
  nand nand_150 (nand_150_out, not_82_out, d_ff_51_q);
  nand nand_151 (nand_151_out, not_83_out, or_28_out);
  nand nand_152 (nand_152_out, not_83_out, d_ff_52_q);
  nand nand_153 (nand_153_out, not_84_out, xor_38_out);
  nand nand_154 (nand_154_out, not_84_out, d_ff_53_q);
  nand nand_155 (nand_155_out, not_85_out, xor_39_out);
  nand nand_156 (nand_156_out, not_85_out, d_ff_54_q);
  nand nand_157 (nand_157_out, not_86_out, xor_40_out);
  nand nand_158 (nand_158_out, not_86_out, d_ff_55_q);
  nand nand_159 (nand_159_out, not_87_out, xor_41_out);
  nand nand_160 (nand_160_out, not_87_out, d_ff_56_q);
  Clock clock_5 (.out(clock_5_out));
  nand nand_161 (nand_161_out, nand_145_out, nand_146_out);
  nand nand_162 (nand_162_out, nand_147_out, nand_148_out);
  nand nand_163 (nand_163_out, nand_149_out, nand_150_out);
  nand nand_164 (nand_164_out, nand_151_out, nand_152_out);
  nand nand_165 (nand_165_out, nand_153_out, nand_154_out);
  nand nand_166 (nand_166_out, nand_155_out, nand_156_out);
  nand nand_167 (nand_167_out, nand_157_out, nand_158_out);
  nand nand_168 (nand_168_out, nand_159_out, nand_160_out);
  D_Flip_Flop d_ff_49 (.clk(clock_5_out), .D(nand_161_out), .Q(d_ff_49_q));  // open: Qn, preset, en, reset
  // AND_Gate and_384 has open pins: in0=and_368_out, in1=d_ff_49_q, out=open
  D_Flip_Flop d_ff_50 (.clk(clock_5_out), .D(nand_162_out), .Q(d_ff_50_q));  // open: Qn, preset, en, reset
  // AND_Gate and_385 has open pins: in0=and_370_out, in1=d_ff_50_q, out=open
  D_Flip_Flop d_ff_51 (.clk(clock_5_out), .D(nand_163_out), .Q(d_ff_51_q));  // open: Qn, preset, en, reset
  // AND_Gate and_386 has open pins: in0=and_372_out, in1=d_ff_51_q, out=open
  D_Flip_Flop d_ff_52 (.clk(clock_5_out), .D(nand_164_out), .Q(d_ff_52_q));  // open: Qn, preset, en, reset
  // AND_Gate and_387 has open pins: in0=and_374_out, in1=d_ff_52_q, out=open
  // AND_Gate and_388 has open pins: in0=and_376_out, in1=d_ff_53_q, out=open
  D_Flip_Flop d_ff_53 (.clk(clock_5_out), .D(nand_165_out), .Q(d_ff_53_q));  // open: Qn, preset, en, reset
  D_Flip_Flop d_ff_54 (.clk(clock_5_out), .D(nand_166_out), .Q(d_ff_54_q));  // open: Qn, preset, en, reset
  // AND_Gate and_389 has open pins: in0=and_378_out, in1=d_ff_54_q, out=open
  D_Flip_Flop d_ff_55 (.clk(clock_5_out), .D(nand_167_out), .Q(d_ff_55_q));  // open: Qn, preset, en, reset
  // AND_Gate and_390 has open pins: in0=and_380_out, in1=d_ff_55_q, out=open
  D_Flip_Flop d_ff_56 (.clk(clock_5_out), .D(nand_168_out), .Q(d_ff_56_q));  // open: Qn, preset, en, reset
  // AND_Gate and_391 has open pins: in0=and_382_out, in1=d_ff_56_q, out=open

  assign Counter_Enable = in_56;
  assign out_83 = A_B;
  assign out_84 = A_B_2;
  assign out_85 = A_B_3;
  assign out_87 = in_30;
  assign out_88 = in_28;
  assign out_89 = in_25;
  assign out_90 = in_24;
  assign out_91 = in_16;
  assign out_92 = in_19;
  assign out_93 = in_20;
  assign out_94 = Address_Line;
  assign out_95 = in_56;
  assign out_104 = ERROR;
  assign Read_5 = in_56;

  // Notes on the sheet:
  //   1
  //   2
  //   3 bit line decoder
  //   Send Instruction
  //   7
  //   6
  //   5
  //   4
  //   Manual Address input
  //   Program Counter
  //   3 separate address jumps
  //   They'll need regsiters too :(
  //   LSB
  //   MSB
  //   Address Input
  //   Jump Address
  //   Program Counter Input
  //   Program Counter Address Output
  //   ROM Registers
  //   Instruction Register
  //   3
  //   2
  //   1
  //   0
  //   Insert Counter New Address
  //   Instruction Line
  //   Instruction Output
  //   Computer On/Off switch
  //   Control Unit
  //   Push Accumulator Value out to ALU
  //   OUTPUT
  //   Accumulator Value going back to ALU
  //   1
  //   2
  //   ALU unit input A
  //   ALU unit input B
  //   Operand
  //   Add
  //   Subtract
  //   Multiply
  //   Divide
  //   Modulo
  //   Not A
  //   Compare
  //   ADd A and B registers
  //   Accumulative Register
  //   Add
  //   Subtract
  //   Multiply
  //   Divide
  //   Modulo
  //   Not A
  //   Compare
  //   Modula
  //   ALU
  //   Add a Nuller for all operations except for multiplication
  //   1
  //   2
  //   Accumulator Register
  //   ERROR
endmodule

module ALU (
  input  MSB,
  input  in_2,
  input  in_3,
  input  in_4,
  input  in_5,
  input  in_6,
  input  in_7,
  input  LSB,
  input  Clear,
  input  Read,
  input  in_11,
  input  Add,
  input  Subtract,
  input  Multiply,
  input  Divide,
  input  Modulo,
  input  And,
  input  Not_A,
  input  Not_B,
  input  Compare,
  input  in_21,
  output out_22,
  output A_B,
  output A_B_2,
  output A_B_3
);

  wire and_1_out, and_2_out, and_3_out, and_4_out, and_5_out, and_6_out, and_7_out, and_8_out, and_9_out,
       and_10_out, and_11_out, and_12_out, and_13_out, and_14_out, and_15_out, and_16_out, and_17_out,
       and_18_out, and_19_out, and_20_out, and_21_out, and_22_out, and_23_out, and_24_out, and_33_out,
       and_34_out, and_35_out, and_36_out, and_37_out, and_38_out, and_39_out, and_40_out, and_41_out,
       and_42_out, and_43_out, and_44_out, and_45_out, and_46_out, and_47_out, and_48_out, and_49_out,
       and_50_out, and_51_out, and_52_out, and_53_out, and_54_out, and_55_out, and_56_out, and_57_out,
       and_58_out, and_59_out, and_60_out, and_61_out, and_62_out, and_63_out, and_64_out, and_65_out,
       and_66_out, and_67_out, and_68_out, and_69_out, and_70_out, and_71_out, and_72_out, and_73_out,
       and_74_out, and_75_out, and_76_out, and_77_out, and_78_out, and_79_out, and_80_out, and_81_out,
       and_82_out, and_83_out, and_84_out, and_85_out, and_86_out, and_87_out, and_88_out, and_89_out,
       and_90_out, and_91_out, and_92_out, and_93_out, and_94_out, and_95_out, and_96_out, and_97_out,
       and_98_out, and_99_out, and_100_out, and_101_out, and_102_out, and_103_out, and_104_out, and_105_out,
       and_106_out, and_107_out, and_108_out, and_109_out, and_110_out, and_111_out, and_112_out,
       and_113_out, and_114_out, and_115_out, and_116_out, and_117_out, and_118_out, and_119_out,
       and_120_out, and_121_out, and_122_out, and_123_out, and_124_out, and_125_out, and_126_out,
       and_127_out, and_128_out, and_129_out, and_130_out, and_131_out, and_133_out, and_134_out,
       and_135_out, and_136_out, and_137_out, and_138_out, and_139_out, and_140_out, and_141_out,
       and_142_out, and_143_out, and_144_out, and_145_out, and_146_out, and_147_out, and_148_out,
       and_149_out, and_150_out, and_151_out, and_152_out, and_153_out, and_154_out, and_155_out,
       and_156_out, and_157_out, and_158_out, and_159_out, clock_1_out, d_ff_1_q, d_ff_2_q, d_ff_3_q,
       d_ff_4_q, d_ff_5_q, d_ff_6_q, d_ff_7_q, d_ff_8_q, nand_1_out, nand_2_out, nand_3_out, nand_4_out,
       nand_5_out, nand_6_out, nand_7_out, nand_8_out, nand_9_out, nand_10_out, nand_11_out, nand_12_out,
       nand_13_out, nand_14_out, nand_15_out, nand_16_out, nand_17_out, nand_18_out, nand_19_out,
       nand_20_out, nand_21_out, nand_22_out, nand_23_out, nand_24_out, nor_1_out, nor_2_out, nor_3_out,
       nor_4_out, not_1_out, not_2_out, not_3_out, not_4_out, not_5_out, not_6_out, not_7_out, not_8_out,
       not_9_out, not_10_out, not_11_out, not_12_out, not_13_out, not_14_out, not_15_out, not_16_out,
       not_17_out, not_18_out, not_19_out, not_20_out, not_21_out, not_22_out, not_23_out, not_24_out,
       not_25_out, not_26_out, not_27_out, not_28_out, or_1_out, or_2_out, or_3_out, or_4_out, or_5_out,
       or_6_out, or_7_out, or_8_out, or_9_out, or_10_out, or_11_out, or_12_out, or_13_out, or_16_out,
       or_17_out, or_18_out, or_19_out, or_20_out, or_21_out, or_22_out, or_23_out, or_24_out, xor_1_out,
       xor_2_out, xor_3_out, xor_4_out, xor_5_out, xor_6_out, xor_7_out, xor_8_out, xor_9_out, xor_10_out,
       xor_11_out, xor_12_out, xor_13_out, xor_14_out, xor_15_out, xor_16_out, xor_17_out, xor_18_out,
       xor_19_out, xor_20_out, xor_21_out, xor_22_out, xor_23_out, xor_24_out, xor_25_out, xor_26_out,
       xor_27_out, xor_28_out, xor_29_out, xor_30_out, xor_31_out, xor_32_out, xor_33_out, xor_34_out,
       xor_35_out, xor_36_out, xor_37_out, xor_38_out, xor_39_out, xor_40_out, xor_41_out;

  and and_1 (and_1_out, Add, LSB);
  and and_2 (and_2_out, Add, in_7);
  and and_3 (and_3_out, Add, in_6);
  and and_4 (and_4_out, Add, in_5);
  and and_5 (and_5_out, Add, in_4);
  and and_6 (and_6_out, Add, in_3);
  and and_7 (and_7_out, Add, in_2);
  and and_8 (and_8_out, Add, MSB);
  and and_9 (and_9_out, LSB, Subtract);
  and and_10 (and_10_out, in_7, Subtract);
  and and_11 (and_11_out, in_6, Subtract);
  and and_12 (and_12_out, in_5, Subtract);
  and and_13 (and_13_out, in_4, Subtract);
  and and_14 (and_14_out, in_3, Subtract);
  and and_15 (and_15_out, in_2, Subtract);
  and and_16 (and_16_out, MSB, Subtract);
  and and_17 (and_17_out, Multiply, LSB);
  and and_18 (and_18_out, Multiply, in_7);
  and and_19 (and_19_out, Multiply, in_6);
  and and_20 (and_20_out, Multiply, in_5);
  and and_21 (and_21_out, Multiply, in_4);
  and and_22 (and_22_out, Multiply, in_3);
  and and_23 (and_23_out, Multiply, in_2);
  and and_24 (and_24_out, Multiply, MSB);
  // AND_Gate and_25 has open pins: in0=Divide, in1=LSB, out=open
  // AND_Gate and_26 has open pins: in0=Divide, in1=in_7, out=open
  // AND_Gate and_27 has open pins: in0=Divide, in1=in_6, out=open
  // AND_Gate and_28 has open pins: in0=Divide, in1=in_5, out=open
  // AND_Gate and_29 has open pins: in0=Divide, in1=in_4, out=open
  // AND_Gate and_30 has open pins: in0=Divide, in1=in_3, out=open
  // AND_Gate and_31 has open pins: in0=Divide, in1=in_2, out=open
  // AND_Gate and_32 has open pins: in0=Divide, in1=MSB, out=open
  not not_1 (not_1_out, and_9_out);
  not not_2 (not_2_out, and_10_out);
  not not_3 (not_3_out, and_11_out);
  not not_4 (not_4_out, and_12_out);
  xor xor_1 (xor_1_out, and_1_out, and_5_out);
  and and_33 (and_33_out, and_5_out, and_1_out);
  xor xor_2 (xor_2_out, and_2_out, and_6_out);
  and and_34 (and_34_out, and_2_out, and_6_out);
  xor xor_3 (xor_3_out, and_3_out, and_7_out);
  and and_35 (and_35_out, and_3_out, and_7_out);
  xor xor_4 (xor_4_out, and_4_out, and_8_out);
  and and_36 (and_36_out, and_4_out, and_8_out);
  xor xor_5 (xor_5_out, not_1_out, and_13_out);
  and and_37 (and_37_out, not_1_out, and_13_out);
  xor xor_6 (xor_6_out, not_2_out, and_14_out);
  and and_38 (and_38_out, not_2_out, and_14_out);
  xor xor_7 (xor_7_out, not_3_out, and_15_out);
  and and_39 (and_39_out, not_3_out, and_15_out);
  xor xor_8 (xor_8_out, not_4_out, and_16_out);
  and and_40 (and_40_out, not_4_out, and_16_out);
  xor xor_9 (xor_9_out, xor_2_out, and_33_out);
  and and_41 (and_41_out, and_33_out, xor_2_out);
  xor xor_10 (xor_10_out, xor_3_out, or_1_out);
  and and_42 (and_42_out, or_1_out, xor_3_out);
  xor xor_11 (xor_11_out, xor_4_out, or_2_out);
  and and_43 (and_43_out, or_2_out, xor_4_out);
  xor xor_12 (xor_12_out, xor_5_out, Subtract);
  and and_44 (and_44_out, Subtract, xor_5_out);
  xor xor_13 (xor_13_out, xor_6_out, or_4_out);
  and and_45 (and_45_out, or_4_out, xor_6_out);
  xor xor_14 (xor_14_out, xor_7_out, or_5_out);
  and and_46 (and_46_out, or_5_out, xor_7_out);
  xor xor_15 (xor_15_out, xor_8_out, or_6_out);
  and and_47 (and_47_out, or_6_out, xor_8_out);
  and and_48 (and_48_out, and_21_out, and_17_out);
  and and_49 (and_49_out, and_21_out, and_18_out);
  and and_50 (and_50_out, and_21_out, and_19_out);
  and and_51 (and_51_out, and_21_out, and_20_out);
  and and_52 (and_52_out, and_22_out, and_17_out);
  and and_53 (and_53_out, and_22_out, and_18_out);
  and and_54 (and_54_out, and_22_out, and_19_out);
  and and_55 (and_55_out, and_22_out, and_20_out);
  and and_56 (and_56_out, and_23_out, and_17_out);
  and and_57 (and_57_out, and_23_out, and_18_out);
  and and_58 (and_58_out, and_23_out, and_19_out);
  and and_59 (and_59_out, and_23_out, and_20_out);
  and and_60 (and_60_out, and_24_out, and_17_out);
  and and_61 (and_61_out, and_24_out, and_18_out);
  and and_62 (and_62_out, and_24_out, and_19_out);
  and and_63 (and_63_out, and_24_out, and_20_out);
  or or_1 (or_1_out, and_41_out, and_34_out);
  or or_2 (or_2_out, and_42_out, and_35_out);
  or or_3 (or_3_out, and_43_out, and_36_out);
  or or_4 (or_4_out, and_44_out, and_37_out);
  or or_5 (or_5_out, and_45_out, and_38_out);
  or or_6 (or_6_out, and_46_out, and_39_out);
  or or_7 (or_7_out, and_47_out, and_40_out);
  and and_64 (and_64_out, xor_12_out, Subtract);
  and and_65 (and_65_out, xor_13_out, Subtract);
  and and_66 (and_66_out, xor_14_out, Subtract);
  and and_67 (and_67_out, Subtract, xor_15_out);
  xor xor_16 (xor_16_out, or_6_out, or_7_out);
  and and_68 (and_68_out, Not_A, LSB);
  and and_69 (and_69_out, Not_A, in_7);
  and and_70 (and_70_out, Not_A, in_6);
  and and_71 (and_71_out, Not_A, in_5);
  and and_72 (and_72_out, Not_A, in_4);
  and and_73 (and_73_out, in_3, Not_A);
  and and_74 (and_74_out, in_2, Not_A);
  and and_75 (and_75_out, MSB, Not_A);
  and and_76 (and_76_out, And, LSB);
  and and_77 (and_77_out, And, in_7);
  and and_78 (and_78_out, And, in_6);
  and and_79 (and_79_out, And, in_5);
  and and_80 (and_80_out, Not_B, in_4);
  and and_81 (and_81_out, Not_B, in_3);
  and and_82 (and_82_out, Not_B, in_2);
  and and_83 (and_83_out, Not_B, MSB);
  and and_84 (and_84_out, Compare, LSB);
  and and_85 (and_85_out, Compare, in_7);
  and and_86 (and_86_out, Compare, in_6);
  and and_87 (and_87_out, Compare, in_5);
  and and_88 (and_88_out, Compare, in_4);
  and and_89 (and_89_out, Compare, in_3);
  and and_90 (and_90_out, Compare, in_2);
  and and_91 (and_91_out, Compare, MSB);
  and and_92 (and_92_out, and_49_out, and_52_out);
  xor xor_17 (xor_17_out, and_53_out, and_50_out);
  and and_93 (and_93_out, and_53_out, and_50_out);
  xor xor_18 (xor_18_out, and_54_out, and_51_out);
  and and_94 (and_94_out, and_54_out, and_51_out);
  xor xor_19 (xor_19_out, and_55_out, in_21);
  and and_95 (and_95_out, and_55_out, in_21);
  and and_96 (and_96_out, and_61_out, and_58_out);
  xor xor_20 (xor_20_out, and_62_out, and_59_out);
  and and_97 (and_97_out, and_62_out, and_59_out);
  and and_98 (and_98_out, and_63_out, in_21);
  not not_5 (not_5_out, and_76_out);
  not not_6 (not_6_out, and_77_out);
  not not_7 (not_7_out, and_78_out);
  not not_8 (not_8_out, and_79_out);
  not not_9 (not_9_out, and_80_out);
  not not_10 (not_10_out, and_81_out);
  not not_11 (not_11_out, and_82_out);
  not not_12 (not_12_out, and_83_out);
  xor xor_21 (xor_21_out, and_52_out, and_49_out);
  xor xor_22 (xor_22_out, xor_18_out, or_9_out);
  and and_99 (and_99_out, or_9_out, xor_18_out);
  xor xor_23 (xor_23_out, and_60_out, and_57_out);
  and and_100 (and_100_out, and_57_out, and_60_out);
  xor xor_24 (xor_24_out, and_61_out, and_58_out);
  and and_101 (and_101_out, or_11_out, xor_20_out);
  xor xor_25 (xor_25_out, and_63_out, in_21);
  and and_102 (and_102_out, and_68_out, and_72_out);
  and and_103 (and_103_out, and_69_out, and_73_out);
  and and_104 (and_104_out, and_70_out, and_74_out);
  and and_105 (and_105_out, and_71_out, and_75_out);
  xor xor_26 (xor_26_out, xor_17_out, and_92_out);
  and and_106 (and_106_out, and_92_out, xor_17_out);
  or or_8 (or_8_out, and_99_out, and_94_out);
  xor xor_27 (xor_27_out, xor_19_out, or_8_out);
  and and_107 (and_107_out, or_8_out, xor_19_out);
  xor xor_28 (xor_28_out, xor_24_out, and_100_out);
  and and_108 (and_108_out, and_100_out, xor_24_out);
  xor xor_29 (xor_29_out, xor_20_out, or_11_out);
  xor xor_30 (xor_30_out, xor_25_out, or_12_out);
  and and_109 (and_109_out, or_12_out, xor_25_out);
  not not_13 (not_13_out, and_87_out);
  not not_14 (not_14_out, and_91_out);
  not not_15 (not_15_out, and_86_out);
  not not_16 (not_16_out, and_90_out);
  not not_17 (not_17_out, and_85_out);
  not not_18 (not_18_out, and_89_out);
  not not_19 (not_19_out, and_84_out);
  not not_20 (not_20_out, and_88_out);
  or or_9 (or_9_out, and_106_out, and_93_out);
  or or_10 (or_10_out, and_107_out, and_95_out);
  or or_11 (or_11_out, and_108_out, and_96_out);
  or or_12 (or_12_out, and_101_out, and_97_out);
  or or_13 (or_13_out, and_109_out, and_98_out);
  and and_110 (and_110_out, not_5_out, And);
  and and_111 (and_111_out, not_6_out, And);
  and and_112 (and_112_out, not_7_out, And);
  and and_113 (and_113_out, not_8_out, And);
  and and_114 (and_114_out, not_9_out, Not_B);
  and and_115 (and_115_out, not_10_out, Not_B);
  and and_116 (and_116_out, not_11_out, Not_B);
  and and_117 (and_117_out, not_12_out, Not_B);
  and and_118 (and_118_out, not_13_out, and_91_out);
  and and_119 (and_119_out, and_87_out, not_14_out);
  and and_120 (and_120_out, not_15_out, and_90_out);
  and and_121 (and_121_out, and_86_out, not_16_out);
  and and_122 (and_122_out, not_17_out, and_89_out);
  and and_123 (and_123_out, and_85_out, not_18_out);
  and and_124 (and_124_out, not_19_out, and_88_out);
  and and_125 (and_125_out, and_84_out, not_20_out);
  nor nor_1 (nor_1_out, and_118_out, and_119_out);
  nor nor_2 (nor_2_out, and_120_out, and_121_out);
  nor nor_3 (nor_3_out, and_122_out, and_123_out);
  nor nor_4 (nor_4_out, and_124_out, and_125_out);
  and and_126 (and_126_out, nor_1_out, and_120_out);
  and and_127 (and_127_out, nor_1_out, and_121_out);
  and and_128 (and_128_out, nor_1_out, nor_2_out, and_122_out);
  and and_129 (and_129_out, nor_1_out, nor_2_out, and_123_out);
  and and_130 (and_130_out, nor_1_out, nor_2_out, nor_3_out, and_124_out);
  and and_131 (and_131_out, nor_1_out, nor_2_out, nor_3_out, and_125_out);
  and and_132 (A_B_3, nor_1_out, nor_2_out, nor_3_out, nor_4_out);
  or or_14 (A_B, and_118_out, and_128_out, and_130_out, and_126_out);
  or or_15 (A_B_2, and_119_out, and_127_out, and_129_out, and_131_out);
  xor xor_31 (xor_31_out, xor_26_out, and_56_out);
  and and_133 (and_133_out, and_56_out, xor_26_out);
  xor xor_32 (xor_32_out, xor_22_out, xor_23_out);
  and and_134 (and_134_out, xor_22_out, xor_23_out);
  xor xor_33 (xor_33_out, xor_27_out, xor_28_out);
  and and_135 (and_135_out, xor_27_out, xor_28_out);
  xor xor_34 (xor_34_out, or_10_out, xor_29_out);
  and and_136 (and_136_out, or_10_out, xor_29_out);
  xor xor_35 (xor_35_out, in_21, xor_30_out);
  and and_137 (and_137_out, in_21, xor_30_out);
  xor xor_36 (xor_36_out, in_21, or_13_out);
  and and_138 (and_138_out, in_21, or_13_out);
  xor xor_37 (xor_37_out, xor_32_out, and_133_out);
  and and_139 (and_139_out, and_133_out, xor_32_out);
  xor xor_38 (xor_38_out, xor_33_out, or_16_out);
  and and_140 (and_140_out, or_16_out, xor_33_out);
  xor xor_39 (xor_39_out, xor_34_out, or_17_out);
  and and_141 (and_141_out, or_17_out, xor_34_out);
  xor xor_40 (xor_40_out, xor_35_out, or_18_out);
  and and_142 (and_142_out, or_18_out, xor_35_out);
  xor xor_41 (xor_41_out, xor_36_out, or_19_out);
  and and_143 (and_143_out, or_19_out, xor_36_out);
  or or_16 (or_16_out, and_139_out, and_134_out);
  or or_17 (or_17_out, and_140_out, and_135_out);
  or or_18 (or_18_out, and_141_out, and_136_out);
  or or_19 (or_19_out, and_142_out, and_137_out);
  or or_20 (or_20_out, and_143_out, and_138_out);
  or or_21 (or_21_out, and_48_out, and_102_out, xor_1_out, and_64_out, and_110_out, and_114_out);
  or or_22 (or_22_out, xor_21_out, and_103_out, xor_9_out, and_65_out, and_111_out, and_112_out);
  or or_23 (or_23_out, xor_31_out, and_104_out, xor_10_out, and_66_out, and_115_out, and_116_out);
  or or_24 (or_24_out, xor_37_out, and_105_out, xor_11_out, and_67_out, and_113_out, and_117_out);
  or or_25 (out_22, or_3_out, xor_16_out, or_20_out);
  and and_144 (and_144_out, Read, in_11);
  not not_21 (not_21_out, and_145_out);
  and and_145 (and_145_out, in_11, Clear);
  and and_146 (and_146_out, Read, in_11);
  not not_22 (not_22_out, and_147_out);
  and and_147 (and_147_out, in_11, Clear);
  and and_148 (and_148_out, Read, in_11);
  not not_23 (not_23_out, and_149_out);
  and and_149 (and_149_out, in_11, Clear);
  and and_150 (and_150_out, Read, in_11);
  and and_151 (and_151_out, in_11, Clear);
  not not_24 (not_24_out, and_151_out);
  and and_152 (and_152_out, Read, Multiply);
  not not_25 (not_25_out, and_153_out);
  and and_153 (and_153_out, Multiply, Clear);
  and and_154 (and_154_out, Read, Multiply);
  and and_155 (and_155_out, Multiply, Clear);
  not not_26 (not_26_out, and_155_out);
  and and_156 (and_156_out, Read, Multiply);
  not not_27 (not_27_out, and_157_out);
  and and_157 (and_157_out, Multiply, Clear);
  and and_158 (and_158_out, Read, Multiply);
  not not_28 (not_28_out, and_159_out);
  and and_159 (and_159_out, Multiply, Clear);
  nand nand_1 (nand_1_out, not_21_out, or_21_out);
  nand nand_2 (nand_2_out, not_21_out, d_ff_1_q);
  nand nand_3 (nand_3_out, not_22_out, or_22_out);
  nand nand_4 (nand_4_out, not_22_out, d_ff_2_q);
  nand nand_5 (nand_5_out, not_23_out, or_23_out);
  nand nand_6 (nand_6_out, not_23_out, d_ff_3_q);
  nand nand_7 (nand_7_out, not_24_out, or_24_out);
  nand nand_8 (nand_8_out, not_24_out, d_ff_4_q);
  nand nand_9 (nand_9_out, not_25_out, xor_38_out);
  nand nand_10 (nand_10_out, not_25_out, d_ff_5_q);
  nand nand_11 (nand_11_out, not_26_out, xor_39_out);
  nand nand_12 (nand_12_out, not_26_out, d_ff_6_q);
  nand nand_13 (nand_13_out, not_27_out, xor_40_out);
  nand nand_14 (nand_14_out, not_27_out, d_ff_7_q);
  nand nand_15 (nand_15_out, not_28_out, xor_41_out);
  nand nand_16 (nand_16_out, not_28_out, d_ff_8_q);
  Clock clock_1 (.out(clock_1_out));
  nand nand_17 (nand_17_out, nand_1_out, nand_2_out);
  nand nand_18 (nand_18_out, nand_3_out, nand_4_out);
  nand nand_19 (nand_19_out, nand_5_out, nand_6_out);
  nand nand_20 (nand_20_out, nand_7_out, nand_8_out);
  nand nand_21 (nand_21_out, nand_9_out, nand_10_out);
  nand nand_22 (nand_22_out, nand_11_out, nand_12_out);
  nand nand_23 (nand_23_out, nand_13_out, nand_14_out);
  nand nand_24 (nand_24_out, nand_15_out, nand_16_out);
  D_Flip_Flop d_ff_1 (.clk(clock_1_out), .D(nand_17_out), .Q(d_ff_1_q));  // open: Qn, preset, en, reset
  // AND_Gate and_160 has open pins: in0=and_144_out, in1=d_ff_1_q, out=open
  D_Flip_Flop d_ff_2 (.clk(clock_1_out), .D(nand_18_out), .Q(d_ff_2_q));  // open: Qn, preset, en, reset
  // AND_Gate and_161 has open pins: in0=and_146_out, in1=d_ff_2_q, out=open
  D_Flip_Flop d_ff_3 (.clk(clock_1_out), .D(nand_19_out), .Q(d_ff_3_q));  // open: Qn, preset, en, reset
  // AND_Gate and_162 has open pins: in0=and_148_out, in1=d_ff_3_q, out=open
  D_Flip_Flop d_ff_4 (.clk(clock_1_out), .D(nand_20_out), .Q(d_ff_4_q));  // open: Qn, preset, en, reset
  // AND_Gate and_163 has open pins: in0=and_150_out, in1=d_ff_4_q, out=open
  // AND_Gate and_164 has open pins: in0=and_152_out, in1=d_ff_5_q, out=open
  D_Flip_Flop d_ff_5 (.clk(clock_1_out), .D(nand_21_out), .Q(d_ff_5_q));  // open: Qn, preset, en, reset
  D_Flip_Flop d_ff_6 (.clk(clock_1_out), .D(nand_22_out), .Q(d_ff_6_q));  // open: Qn, preset, en, reset
  // AND_Gate and_165 has open pins: in0=and_154_out, in1=d_ff_6_q, out=open
  D_Flip_Flop d_ff_7 (.clk(clock_1_out), .D(nand_23_out), .Q(d_ff_7_q));  // open: Qn, preset, en, reset
  // AND_Gate and_166 has open pins: in0=and_156_out, in1=d_ff_7_q, out=open
  // AND_Gate and_167 has open pins: in0=and_158_out, in1=d_ff_8_q, out=open
  D_Flip_Flop d_ff_8 (.clk(clock_1_out), .D(nand_24_out), .Q(d_ff_8_q));  // open: Qn, preset, en, reset

  // Notes on the sheet:
  //   Modula
  //   ALU
  //   Add a Nuller for all operations except for multiplication
  //   1
  //   2
  //   Accumulator Register
  //   ERROR
endmodule

module Program_Counter (
  input  Clear_Counter,
  input  Enable_Counter,
  input  in_3,
  input  in_4,
  input  in_5,
  input  in_6,
  input  in_7,
  input  in_8,
  input  in_9,
  input  in_10,
  input  in_11,
  output out_12,
  output out_13,
  output out_14,
  output out_15,
  output out_16,
  output out_17,
  output out_18,
  output out_19,
  output out_20
);

  wire and_1_out, and_2_out, and_3_out, and_4_out, and_5_out, and_6_out, and_7_out, and_8_out, and_9_out,
       and_10_out, and_11_out, and_12_out, and_13_out, and_14_out, and_15_out, clock_1_out;

  Clock clock_1 (.out(clock_1_out));
  J_K_Flip_Flop #(.trigger("falling")) j_k_ff_1 (
    .J(Enable_Counter), .clk(clock_1_out), .K(Enable_Counter), .Q(out_12), .preset(and_2_out),
    .reset(Clear_Counter));  // open: Qn, en
  and and_1 (and_1_out, Enable_Counter, out_12);
  and and_2 (and_2_out, in_3, in_4);
  and and_3 (and_3_out, in_3, in_5);
  and and_4 (and_4_out, in_3, in_6);
  and and_5 (and_5_out, in_3, in_7);
  and and_6 (and_6_out, in_3, in_8);
  and and_7 (and_7_out, in_3, in_9);
  and and_8 (and_8_out, in_3, in_10);
  and and_9 (and_9_out, in_3, in_11);
  J_K_Flip_Flop #(.trigger("falling")) j_k_ff_2 (
    .J(and_1_out), .clk(clock_1_out), .K(and_1_out), .Q(out_13), .preset(and_3_out), .reset(Clear_Counter));  // open: Qn, en
  and and_10 (and_10_out, and_1_out, out_13);
  J_K_Flip_Flop #(.trigger("falling")) j_k_ff_3 (
    .J(and_10_out), .clk(clock_1_out), .K(and_10_out), .Q(out_14), .preset(and_4_out), .reset(Clear_Counter));  // open: Qn, en
  and and_11 (and_11_out, and_10_out, out_14);
  J_K_Flip_Flop #(.trigger("falling")) j_k_ff_4 (
    .J(and_11_out), .clk(clock_1_out), .K(and_11_out), .Q(out_15), .preset(and_5_out), .reset(Clear_Counter));  // open: Qn, en
  and and_12 (and_12_out, and_11_out, out_15);
  J_K_Flip_Flop #(.trigger("falling")) j_k_ff_5 (
    .J(and_12_out), .clk(clock_1_out), .K(and_12_out), .Q(out_16), .preset(and_6_out), .reset(Clear_Counter));  // open: Qn, en
  and and_13 (and_13_out, and_12_out, out_16);
  J_K_Flip_Flop #(.trigger("falling")) j_k_ff_6 (
    .J(and_13_out), .clk(clock_1_out), .K(and_13_out), .Q(out_17), .preset(and_7_out), .reset(Clear_Counter));  // open: Qn, en
  and and_14 (and_14_out, and_13_out, out_17);
  J_K_Flip_Flop #(.trigger("falling")) j_k_ff_7 (
    .J(and_14_out), .clk(clock_1_out), .K(and_14_out), .Q(out_18), .preset(and_8_out), .reset(Clear_Counter));  // open: Qn, en
  and and_15 (and_15_out, and_14_out, out_18);
  J_K_Flip_Flop #(.trigger("falling")) j_k_ff_8 (
    .J(and_15_out), .clk(clock_1_out), .K(and_15_out), .Q(out_19), .preset(and_9_out), .reset(Clear_Counter));  // open: Qn, en
  and and_16 (out_20, and_15_out, out_19);

  // Notes on the sheet:
  //   Send Instruction
  //   Program Counter
  //   Manual Address input
endmodule

module ROM (
  input  in_1,
  input  Input,
  input  Clear,
  input  Read,
  input  in_5,
  input  in_6,
  input  in_7,
  input  Address,
  input  _0_7,
  output out_10,
  output out_11,
  output out_12,
  output out_13
);

  wire and_1_out, and_2_out, and_3_out, and_4_out, and_5_out, and_6_out, and_7_out, and_8_out, and_9_out,
       and_10_out, and_11_out, and_12_out, and_13_out, and_14_out, and_15_out, and_16_out, and_17_out,
       and_18_out, and_19_out, and_20_out, and_21_out, and_22_out, and_23_out, and_24_out, and_25_out,
       and_26_out, and_27_out, and_28_out, and_29_out, and_30_out, and_31_out, and_32_out, and_33_out,
       and_34_out, and_35_out, and_36_out, and_37_out, and_38_out, and_39_out, and_40_out, and_41_out,
       and_42_out, and_43_out, and_44_out, and_45_out, and_46_out, and_47_out, and_48_out, and_49_out,
       and_50_out, and_51_out, and_52_out, and_53_out, and_54_out, and_55_out, and_56_out, and_57_out,
       and_58_out, and_59_out, and_60_out, and_61_out, and_62_out, and_63_out, and_64_out, and_65_out,
       and_66_out, and_67_out, and_68_out, and_69_out, and_70_out, and_71_out, and_72_out, and_73_out,
       and_74_out, and_75_out, and_76_out, and_77_out, and_78_out, and_79_out, and_80_out, and_81_out,
       and_82_out, and_83_out, and_84_out, and_85_out, and_86_out, and_87_out, and_88_out, and_89_out,
       and_90_out, and_91_out, and_92_out, and_93_out, and_94_out, and_95_out, and_96_out, and_97_out,
       and_98_out, and_99_out, and_100_out, and_101_out, and_102_out, and_103_out, and_104_out, and_105_out,
       and_106_out, and_107_out, and_108_out, and_109_out, and_110_out, and_111_out, and_112_out,
       clock_1_out, d_ff_1_q, d_ff_2_q, d_ff_3_q, d_ff_4_q, d_ff_5_q, d_ff_6_q, d_ff_7_q, d_ff_8_q, d_ff_9_q,
       d_ff_10_q, d_ff_11_q, d_ff_12_q, d_ff_13_q, d_ff_14_q, d_ff_15_q, d_ff_16_q, d_ff_17_q, d_ff_18_q,
       d_ff_19_q, d_ff_20_q, d_ff_21_q, d_ff_22_q, d_ff_23_q, d_ff_24_q, d_ff_25_q, d_ff_26_q, d_ff_27_q,
       d_ff_28_q, d_ff_29_q, d_ff_30_q, d_ff_31_q, d_ff_32_q, nand_1_out, nand_2_out, nand_3_out, nand_4_out,
       nand_5_out, nand_6_out, nand_7_out, nand_8_out, nand_9_out, nand_10_out, nand_11_out, nand_12_out,
       nand_13_out, nand_14_out, nand_15_out, nand_16_out, nand_17_out, nand_18_out, nand_19_out,
       nand_20_out, nand_21_out, nand_22_out, nand_23_out, nand_24_out, nand_25_out, nand_26_out,
       nand_27_out, nand_28_out, nand_29_out, nand_30_out, nand_31_out, nand_32_out, nand_33_out,
       nand_34_out, nand_35_out, nand_36_out, nand_37_out, nand_38_out, nand_39_out, nand_40_out,
       nand_41_out, nand_42_out, nand_43_out, nand_44_out, nand_45_out, nand_46_out, nand_47_out,
       nand_48_out, nand_49_out, nand_50_out, nand_51_out, nand_52_out, nand_53_out, nand_54_out,
       nand_55_out, nand_56_out, nand_57_out, nand_58_out, nand_59_out, nand_60_out, nand_61_out,
       nand_62_out, nand_63_out, nand_64_out, nand_65_out, nand_66_out, nand_67_out, nand_68_out,
       nand_69_out, nand_70_out, nand_71_out, nand_72_out, nand_73_out, nand_74_out, nand_75_out,
       nand_76_out, nand_77_out, nand_78_out, nand_79_out, nand_80_out, nand_81_out, nand_82_out,
       nand_83_out, nand_84_out, nand_85_out, nand_86_out, nand_87_out, nand_88_out, nand_89_out,
       nand_90_out, nand_91_out, nand_92_out, nand_93_out, nand_94_out, nand_95_out, nand_96_out, not_1_out,
       not_2_out, not_3_out, not_4_out, not_5_out, not_6_out, not_7_out, not_8_out, not_9_out, not_10_out,
       not_11_out, not_12_out, not_13_out, not_14_out, not_15_out, not_16_out, not_17_out, not_18_out,
       not_19_out, not_20_out, not_21_out, not_22_out, not_23_out, not_24_out, not_25_out, not_26_out,
       not_27_out, not_28_out, not_29_out, not_30_out, not_31_out, not_32_out, not_33_out, not_34_out,
       not_35_out;

  not not_1 (not_1_out, in_7);
  not not_2 (not_2_out, Address);
  not not_3 (not_3_out, _0_7);
  and and_1 (and_1_out, _0_7, and_2_out);
  and and_2 (and_2_out, in_7, Address);
  and and_3 (and_3_out, in_7, and_4_out);
  and and_4 (and_4_out, Address, not_3_out);
  and and_5 (and_5_out, in_7, and_6_out);
  and and_6 (and_6_out, _0_7, not_2_out);
  and and_7 (and_7_out, in_7, and_8_out);
  and and_8 (and_8_out, not_3_out, not_2_out);
  and and_9 (and_9_out, _0_7, and_10_out);
  and and_10 (and_10_out, Address, not_1_out);
  and and_11 (and_11_out, Address, and_12_out);
  and and_12 (and_12_out, not_1_out, not_3_out);
  and and_13 (and_13_out, _0_7, and_14_out);
  and and_14 (and_14_out, not_1_out, not_2_out);
  and and_15 (and_15_out, and_16_out, not_3_out);
  and and_16 (and_16_out, not_1_out, not_2_out);
  and and_17 (and_17_out, Read, and_1_out);
  and and_18 (and_18_out, and_1_out, Clear);
  and and_19 (and_19_out, Read, and_1_out);
  and and_20 (and_20_out, and_1_out, Clear);
  and and_21 (and_21_out, Read, and_1_out);
  and and_22 (and_22_out, and_1_out, Clear);
  and and_23 (and_23_out, Read, and_1_out);
  and and_24 (and_24_out, and_1_out, Clear);
  and and_25 (and_25_out, Read, and_3_out);
  and and_26 (and_26_out, and_3_out, Clear);
  and and_27 (and_27_out, Read, and_3_out);
  and and_28 (and_28_out, and_3_out, Clear);
  and and_29 (and_29_out, Read, and_3_out);
  and and_30 (and_30_out, and_3_out, Clear);
  and and_31 (and_31_out, Read, and_3_out);
  and and_32 (and_32_out, and_3_out, Clear);
  and and_33 (and_33_out, Read, and_5_out);
  and and_34 (and_34_out, and_5_out, Clear);
  and and_35 (and_35_out, Read, and_5_out);
  and and_36 (and_36_out, and_5_out, Clear);
  and and_37 (and_37_out, Read, and_5_out);
  and and_38 (and_38_out, and_5_out, Clear);
  and and_39 (and_39_out, Read, and_5_out);
  and and_40 (and_40_out, and_5_out, Clear);
  and and_41 (and_41_out, Read, and_7_out);
  and and_42 (and_42_out, and_7_out, Clear);
  and and_43 (and_43_out, Read, and_7_out);
  and and_44 (and_44_out, and_7_out, Clear);
  and and_45 (and_45_out, Read, and_7_out);
  and and_46 (and_46_out, and_7_out, Clear);
  and and_47 (and_47_out, Read, and_7_out);
  and and_48 (and_48_out, and_7_out, Clear);
  not not_4 (not_4_out, and_18_out);
  not not_5 (not_5_out, and_20_out);
  not not_6 (not_6_out, and_22_out);
  not not_7 (not_7_out, and_24_out);
  not not_8 (not_8_out, and_26_out);
  not not_9 (not_9_out, and_28_out);
  not not_10 (not_10_out, and_30_out);
  not not_11 (not_11_out, and_32_out);
  not not_12 (not_12_out, and_34_out);
  not not_13 (not_13_out, and_36_out);
  not not_14 (not_14_out, and_38_out);
  not not_15 (not_15_out, and_40_out);
  not not_16 (not_16_out, and_42_out);
  not not_17 (not_17_out, and_44_out);
  not not_18 (not_18_out, and_46_out);
  not not_19 (not_19_out, and_48_out);
  nand nand_1 (nand_1_out, not_4_out, in_1);
  nand nand_2 (nand_2_out, not_4_out, d_ff_1_q);
  nand nand_3 (nand_3_out, not_5_out, Input);
  nand nand_4 (nand_4_out, not_5_out, d_ff_2_q);
  nand nand_5 (nand_5_out, not_6_out, in_5);
  nand nand_6 (nand_6_out, not_6_out, d_ff_3_q);
  nand nand_7 (nand_7_out, not_7_out, in_6);
  nand nand_8 (nand_8_out, not_7_out, d_ff_4_q);
  nand nand_9 (nand_9_out, not_8_out, in_1);
  nand nand_10 (nand_10_out, not_8_out, d_ff_5_q);
  nand nand_11 (nand_11_out, not_9_out, Input);
  nand nand_12 (nand_12_out, not_9_out, d_ff_6_q);
  nand nand_13 (nand_13_out, not_10_out, in_5);
  nand nand_14 (nand_14_out, not_10_out, d_ff_7_q);
  nand nand_15 (nand_15_out, not_11_out, in_6);
  nand nand_16 (nand_16_out, not_11_out, d_ff_8_q);
  nand nand_17 (nand_17_out, not_12_out, in_1);
  nand nand_18 (nand_18_out, not_12_out, d_ff_9_q);
  nand nand_19 (nand_19_out, not_13_out, Input);
  nand nand_20 (nand_20_out, not_13_out, d_ff_10_q);
  nand nand_21 (nand_21_out, not_14_out, in_5);
  nand nand_22 (nand_22_out, not_14_out, d_ff_11_q);
  nand nand_23 (nand_23_out, not_15_out, in_6);
  nand nand_24 (nand_24_out, not_15_out, d_ff_12_q);
  nand nand_25 (nand_25_out, not_16_out, in_1);
  nand nand_26 (nand_26_out, not_16_out, d_ff_13_q);
  nand nand_27 (nand_27_out, not_17_out, Input);
  nand nand_28 (nand_28_out, not_17_out, d_ff_14_q);
  nand nand_29 (nand_29_out, not_18_out, in_5);
  nand nand_30 (nand_30_out, not_18_out, d_ff_15_q);
  nand nand_31 (nand_31_out, not_19_out, in_6);
  nand nand_32 (nand_32_out, not_19_out, d_ff_16_q);
  Clock clock_1 (.out(clock_1_out));
  D_Flip_Flop d_ff_1 (.clk(clock_1_out), .D(nand_33_out), .Q(d_ff_1_q));  // open: Qn, preset, en, reset
  nand nand_33 (nand_33_out, nand_1_out, nand_2_out);
  D_Flip_Flop d_ff_2 (.clk(clock_1_out), .D(nand_34_out), .Q(d_ff_2_q));  // open: Qn, preset, en, reset
  nand nand_34 (nand_34_out, nand_3_out, nand_4_out);
  D_Flip_Flop d_ff_3 (.clk(clock_1_out), .D(nand_35_out), .Q(d_ff_3_q));  // open: Qn, preset, en, reset
  nand nand_35 (nand_35_out, nand_5_out, nand_6_out);
  D_Flip_Flop d_ff_4 (.clk(clock_1_out), .D(nand_36_out), .Q(d_ff_4_q));  // open: Qn, preset, en, reset
  nand nand_36 (nand_36_out, nand_7_out, nand_8_out);
  D_Flip_Flop d_ff_5 (.clk(clock_1_out), .D(nand_37_out), .Q(d_ff_5_q));  // open: Qn, preset, en, reset
  nand nand_37 (nand_37_out, nand_9_out, nand_10_out);
  D_Flip_Flop d_ff_6 (.clk(clock_1_out), .D(nand_38_out), .Q(d_ff_6_q));  // open: Qn, preset, en, reset
  nand nand_38 (nand_38_out, nand_11_out, nand_12_out);
  D_Flip_Flop d_ff_7 (.clk(clock_1_out), .D(nand_39_out), .Q(d_ff_7_q));  // open: Qn, preset, en, reset
  nand nand_39 (nand_39_out, nand_13_out, nand_14_out);
  D_Flip_Flop d_ff_8 (.clk(clock_1_out), .D(nand_40_out), .Q(d_ff_8_q));  // open: Qn, preset, en, reset
  nand nand_40 (nand_40_out, nand_15_out, nand_16_out);
  D_Flip_Flop d_ff_9 (.clk(clock_1_out), .D(nand_41_out), .Q(d_ff_9_q));  // open: Qn, preset, en, reset
  nand nand_41 (nand_41_out, nand_17_out, nand_18_out);
  D_Flip_Flop d_ff_10 (.clk(clock_1_out), .D(nand_42_out), .Q(d_ff_10_q));  // open: Qn, preset, en, reset
  nand nand_42 (nand_42_out, nand_19_out, nand_20_out);
  D_Flip_Flop d_ff_11 (.clk(clock_1_out), .D(nand_43_out), .Q(d_ff_11_q));  // open: Qn, preset, en, reset
  nand nand_43 (nand_43_out, nand_21_out, nand_22_out);
  D_Flip_Flop d_ff_12 (.clk(clock_1_out), .D(nand_44_out), .Q(d_ff_12_q));  // open: Qn, preset, en, reset
  nand nand_44 (nand_44_out, nand_23_out, nand_24_out);
  D_Flip_Flop d_ff_13 (.clk(clock_1_out), .D(nand_45_out), .Q(d_ff_13_q));  // open: Qn, preset, en, reset
  nand nand_45 (nand_45_out, nand_25_out, nand_26_out);
  D_Flip_Flop d_ff_14 (.clk(clock_1_out), .D(nand_46_out), .Q(d_ff_14_q));  // open: Qn, preset, en, reset
  nand nand_46 (nand_46_out, nand_27_out, nand_28_out);
  D_Flip_Flop d_ff_15 (.clk(clock_1_out), .D(nand_47_out), .Q(d_ff_15_q));  // open: Qn, preset, en, reset
  nand nand_47 (nand_47_out, nand_29_out, nand_30_out);
  D_Flip_Flop d_ff_16 (.clk(clock_1_out), .D(nand_48_out), .Q(d_ff_16_q));  // open: Qn, preset, en, reset
  nand nand_48 (nand_48_out, nand_31_out, nand_32_out);
  and and_49 (and_49_out, and_17_out, d_ff_1_q);
  and and_50 (and_50_out, and_19_out, d_ff_2_q);
  and and_51 (and_51_out, and_21_out, d_ff_3_q);
  and and_52 (and_52_out, and_23_out, d_ff_4_q);
  and and_53 (and_53_out, and_25_out, d_ff_5_q);
  and and_54 (and_54_out, and_27_out, d_ff_6_q);
  and and_55 (and_55_out, and_29_out, d_ff_7_q);
  and and_56 (and_56_out, and_31_out, d_ff_8_q);
  and and_57 (and_57_out, and_33_out, d_ff_9_q);
  and and_58 (and_58_out, and_35_out, d_ff_10_q);
  and and_59 (and_59_out, and_37_out, d_ff_11_q);
  and and_60 (and_60_out, and_39_out, d_ff_12_q);
  and and_61 (and_61_out, and_41_out, d_ff_13_q);
  and and_62 (and_62_out, and_43_out, d_ff_14_q);
  and and_63 (and_63_out, and_45_out, d_ff_15_q);
  and and_64 (and_64_out, and_47_out, d_ff_16_q);
  and and_65 (and_65_out, Read, and_9_out);
  and and_66 (and_66_out, and_9_out, Clear);
  not not_20 (not_20_out, and_66_out);
  and and_67 (and_67_out, Read, and_9_out);
  not not_21 (not_21_out, and_68_out);
  and and_68 (and_68_out, and_9_out, Clear);
  and and_69 (and_69_out, Read, and_9_out);
  not not_22 (not_22_out, and_70_out);
  and and_70 (and_70_out, and_9_out, Clear);
  and and_71 (and_71_out, Read, and_9_out);
  and and_72 (and_72_out, and_9_out, Clear);
  not not_23 (not_23_out, and_72_out);
  and and_73 (and_73_out, Read, and_11_out);
  and and_74 (and_74_out, and_11_out, Clear);
  not not_24 (not_24_out, and_74_out);
  and and_75 (and_75_out, Read, and_11_out);
  and and_76 (and_76_out, and_11_out, Clear);
  not not_25 (not_25_out, and_76_out);
  and and_77 (and_77_out, Read, and_11_out);
  not not_26 (not_26_out, and_78_out);
  and and_78 (and_78_out, and_11_out, Clear);
  and and_79 (and_79_out, Read, and_11_out);
  not not_27 (not_27_out, and_80_out);
  and and_80 (and_80_out, and_11_out, Clear);
  and and_81 (and_81_out, Read, and_13_out);
  not not_28 (not_28_out, and_82_out);
  and and_82 (and_82_out, and_13_out, Clear);
  and and_83 (and_83_out, Read, and_13_out);
  and and_84 (and_84_out, and_13_out, Clear);
  not not_29 (not_29_out, and_84_out);
  and and_85 (and_85_out, Read, and_13_out);
  and and_86 (and_86_out, and_13_out, Clear);
  not not_30 (not_30_out, and_86_out);
  and and_87 (and_87_out, Read, and_13_out);
  not not_31 (not_31_out, and_88_out);
  and and_88 (and_88_out, and_13_out, Clear);
  and and_89 (and_89_out, Read, and_15_out);
  and and_90 (and_90_out, and_15_out, Clear);
  not not_32 (not_32_out, and_90_out);
  and and_91 (and_91_out, Read, and_15_out);
  not not_33 (not_33_out, and_92_out);
  and and_92 (and_92_out, and_15_out, Clear);
  and and_93 (and_93_out, Read, and_15_out);
  and and_94 (and_94_out, and_15_out, Clear);
  not not_34 (not_34_out, and_94_out);
  and and_95 (and_95_out, Read, and_15_out);
  and and_96 (and_96_out, and_15_out, Clear);
  not not_35 (not_35_out, and_96_out);
  nand nand_49 (nand_49_out, not_20_out, in_1);
  nand nand_50 (nand_50_out, not_20_out, d_ff_17_q);
  nand nand_51 (nand_51_out, not_21_out, Input);
  nand nand_52 (nand_52_out, not_21_out, d_ff_18_q);
  nand nand_53 (nand_53_out, not_22_out, in_5);
  nand nand_54 (nand_54_out, not_22_out, d_ff_19_q);
  nand nand_55 (nand_55_out, not_23_out, in_6);
  nand nand_56 (nand_56_out, not_23_out, d_ff_20_q);
  nand nand_57 (nand_57_out, not_24_out, in_1);
  nand nand_58 (nand_58_out, not_24_out, d_ff_21_q);
  nand nand_59 (nand_59_out, not_25_out, Input);
  nand nand_60 (nand_60_out, not_25_out, d_ff_22_q);
  nand nand_61 (nand_61_out, not_26_out, in_5);
  nand nand_62 (nand_62_out, not_26_out, d_ff_23_q);
  nand nand_63 (nand_63_out, not_27_out, in_6);
  nand nand_64 (nand_64_out, not_27_out, d_ff_24_q);
  nand nand_65 (nand_65_out, not_28_out, in_1);
  nand nand_66 (nand_66_out, not_28_out, d_ff_25_q);
  nand nand_67 (nand_67_out, not_29_out, Input);
  nand nand_68 (nand_68_out, not_29_out, d_ff_26_q);
  nand nand_69 (nand_69_out, not_30_out, in_5);
  nand nand_70 (nand_70_out, not_30_out, d_ff_27_q);
  nand nand_71 (nand_71_out, not_31_out, in_6);
  nand nand_72 (nand_72_out, not_31_out, d_ff_28_q);
  nand nand_73 (nand_73_out, not_32_out, in_1);
  nand nand_74 (nand_74_out, not_32_out, d_ff_29_q);
  nand nand_75 (nand_75_out, not_33_out, Input);
  nand nand_76 (nand_76_out, not_33_out, d_ff_30_q);
  nand nand_77 (nand_77_out, not_34_out, in_5);
  nand nand_78 (nand_78_out, not_34_out, d_ff_31_q);
  nand nand_79 (nand_79_out, not_35_out, in_6);
  nand nand_80 (nand_80_out, not_35_out, d_ff_32_q);
  nand nand_81 (nand_81_out, nand_49_out, nand_50_out);
  nand nand_82 (nand_82_out, nand_51_out, nand_52_out);
  nand nand_83 (nand_83_out, nand_53_out, nand_54_out);
  nand nand_84 (nand_84_out, nand_55_out, nand_56_out);
  nand nand_85 (nand_85_out, nand_57_out, nand_58_out);
  nand nand_86 (nand_86_out, nand_59_out, nand_60_out);
  nand nand_87 (nand_87_out, nand_61_out, nand_62_out);
  nand nand_88 (nand_88_out, nand_63_out, nand_64_out);
  nand nand_89 (nand_89_out, nand_65_out, nand_66_out);
  nand nand_90 (nand_90_out, nand_67_out, nand_68_out);
  nand nand_91 (nand_91_out, nand_69_out, nand_70_out);
  nand nand_92 (nand_92_out, nand_71_out, nand_72_out);
  nand nand_93 (nand_93_out, nand_73_out, nand_74_out);
  nand nand_94 (nand_94_out, nand_75_out, nand_76_out);
  nand nand_95 (nand_95_out, nand_77_out, nand_78_out);
  nand nand_96 (nand_96_out, nand_79_out, nand_80_out);
  D_Flip_Flop d_ff_17 (.clk(clock_1_out), .D(nand_81_out), .Q(d_ff_17_q));  // open: Qn, preset, en, reset
  and and_97 (and_97_out, and_65_out, d_ff_17_q);
  D_Flip_Flop d_ff_18 (.clk(clock_1_out), .D(nand_82_out), .Q(d_ff_18_q));  // open: Qn, preset, en, reset
  and and_98 (and_98_out, and_67_out, d_ff_18_q);
  D_Flip_Flop d_ff_19 (.clk(clock_1_out), .D(nand_83_out), .Q(d_ff_19_q));  // open: Qn, preset, en, reset
  and and_99 (and_99_out, and_69_out, d_ff_19_q);
  D_Flip_Flop d_ff_20 (.clk(clock_1_out), .D(nand_84_out), .Q(d_ff_20_q));  // open: Qn, preset, en, reset
  and and_100 (and_100_out, and_71_out, d_ff_20_q);
  D_Flip_Flop d_ff_21 (.clk(clock_1_out), .D(nand_85_out), .Q(d_ff_21_q));  // open: Qn, preset, en, reset
  and and_101 (and_101_out, and_73_out, d_ff_21_q);
  D_Flip_Flop d_ff_22 (.clk(clock_1_out), .D(nand_86_out), .Q(d_ff_22_q));  // open: Qn, preset, en, reset
  and and_102 (and_102_out, and_75_out, d_ff_22_q);
  D_Flip_Flop d_ff_23 (.clk(clock_1_out), .D(nand_87_out), .Q(d_ff_23_q));  // open: Qn, preset, en, reset
  and and_103 (and_103_out, and_77_out, d_ff_23_q);
  D_Flip_Flop d_ff_24 (.clk(clock_1_out), .D(nand_88_out), .Q(d_ff_24_q));  // open: Qn, preset, en, reset
  and and_104 (and_104_out, and_79_out, d_ff_24_q);
  D_Flip_Flop d_ff_25 (.clk(clock_1_out), .D(nand_89_out), .Q(d_ff_25_q));  // open: Qn, preset, en, reset
  and and_105 (and_105_out, and_81_out, d_ff_25_q);
  D_Flip_Flop d_ff_26 (.clk(clock_1_out), .D(nand_90_out), .Q(d_ff_26_q));  // open: Qn, preset, en, reset
  and and_106 (and_106_out, and_83_out, d_ff_26_q);
  D_Flip_Flop d_ff_27 (.clk(clock_1_out), .D(nand_91_out), .Q(d_ff_27_q));  // open: Qn, preset, en, reset
  and and_107 (and_107_out, and_85_out, d_ff_27_q);
  D_Flip_Flop d_ff_28 (.clk(clock_1_out), .D(nand_92_out), .Q(d_ff_28_q));  // open: Qn, preset, en, reset
  and and_108 (and_108_out, and_87_out, d_ff_28_q);
  D_Flip_Flop d_ff_29 (.clk(clock_1_out), .D(nand_93_out), .Q(d_ff_29_q));  // open: Qn, preset, en, reset
  and and_109 (and_109_out, and_89_out, d_ff_29_q);
  D_Flip_Flop d_ff_30 (.clk(clock_1_out), .D(nand_94_out), .Q(d_ff_30_q));  // open: Qn, preset, en, reset
  and and_110 (and_110_out, and_91_out, d_ff_30_q);
  D_Flip_Flop d_ff_31 (.clk(clock_1_out), .D(nand_95_out), .Q(d_ff_31_q));  // open: Qn, preset, en, reset
  and and_111 (and_111_out, and_93_out, d_ff_31_q);
  D_Flip_Flop d_ff_32 (.clk(clock_1_out), .D(nand_96_out), .Q(d_ff_32_q));  // open: Qn, preset, en, reset
  and and_112 (and_112_out, and_95_out, d_ff_32_q);
  or or_1 (out_10, and_49_out, and_97_out, and_53_out, and_57_out, and_61_out, and_101_out, and_105_out, and_109_out);
  or or_2 (out_11, and_50_out, and_98_out, and_110_out, and_54_out, and_58_out, and_62_out, and_102_out, and_106_out);
  or or_3 (out_12, and_51_out, and_55_out, and_59_out, and_63_out, and_99_out, and_103_out, and_107_out, and_111_out);
  or or_4 (out_13, and_52_out, and_56_out, and_60_out, and_64_out, and_100_out, and_104_out, and_108_out, and_112_out);

  // Notes on the sheet:
  //   3 bit line decoder
  //   7
  //   6
  //   5
  //   4
  //   3
  //   2
  //   1
  //   0
endmodule
module Control_Unit (
  input  in_1,
  input  in_2,
  input  in_3,
  input  Address_Line,
  input  in_5,
  input  in_6,
  input  in_7,
  input  in_8,
  input  in_9,
  input  LSB,
  input  in_11,
  input  in_12,
  input  ALU_output,
  input  in_14,
  input  in_15,
  input  MSB,
  input  ERROR,
  input  A_B,
  input  A_B_2,
  input  A_B_3,
  input  in_21,
  input  in_22,
  input  in_23,
  input  in_24,
  input  in_25,
  input  in_26,
  input  in_27,
  input  Read,
  input  in_29,
  output out_30,
  output LSB_2,
  output out_32,
  output out_33,
  output out_34,
  output out_35,
  output out_36,
  output LSB_3,
  output out_38,
  output MSB_2,
  output out_40,
  output out_41,
  output Counter_Enable,
  output MSB_3,
  output Counter_Clear,
  output LSB_4,
  output out_46,
  output out_47,
  output MSB_4,
  output Add,
  output Subtract,
  output Multiply,
  output Divide,
  output Modulo,
  output Not_A,
  output Compare,
  output Do_NOTHING,
  output out_57,
  output out_58,
  output out_59,
  output Read_2,
  output out_61,
  output out_62,
  output out_63,
  output out_64,
  output out_65,
  output out_66,
  output out_67,
  output out_68,
  output out_69,
  output LSB_5,
  output out_71,
  output out_72,
  output out_73,
  output out_74,
  output out_75,
  output MSB_5,
  output out_77,
  output out_78
);

  wire and_9_out, and_10_out, and_12_out, and_13_out, and_15_out, and_32_out, and_34_out, and_35_out,
       and_36_out, not_1_out, not_2_out, not_3_out, not_4_out, not_5_out, not_6_out, not_7_out, not_8_out;

  and and_1 (LSB_2, Read, and_15_out);
  and and_2 (out_32, in_27, and_15_out);
  and and_3 (out_33, in_26, and_15_out);
  and and_4 (out_34, in_25, and_15_out);
  and and_5 (out_35, Read, and_12_out);
  and and_6 (out_36, in_27, and_12_out);
  and and_7 (out_38, in_26, and_12_out);
  and and_8 (MSB_2, in_25, and_12_out);
  and and_9 (and_9_out, in_21, in_22, in_23, in_24);
  and and_10 (and_10_out, not_1_out, in_22, in_23, in_24);
  and and_11 (Counter_Clear, not_4_out, in_21, in_23, in_24);
  and and_12 (and_12_out, not_1_out, not_4_out, in_23, in_24);
  and and_13 (and_13_out, not_2_out, in_21, in_22, in_24);
  and and_14 (in_12, not_1_out, not_2_out, in_22, in_24);
  and and_15 (and_15_out, not_4_out, not_2_out, in_21, in_24);
  and and_16 (LSB, not_1_out, not_4_out, not_2_out, in_24);
  not not_1 (not_1_out, in_21);
  not not_2 (not_2_out, in_23);
  not not_3 (not_3_out, in_24);
  not not_4 (not_4_out, in_22);
  and and_17 (out_30, in_23, in_22, not_3_out, in_21);
  and and_18 (Not_A, in_23, in_22, not_3_out, not_1_out);
  and and_19 (Modulo, in_23, in_21, not_3_out, not_4_out);
  and and_20 (Divide, in_23, not_4_out, not_3_out, not_1_out);
  and and_21 (Multiply, in_21, in_22, not_3_out, not_2_out);
  and and_22 (Subtract, in_22, not_3_out, not_2_out, not_1_out);
  and and_23 (Add, not_3_out, not_2_out, not_4_out, in_21);
  and and_24 (Do_NOTHING, not_3_out, not_2_out, not_4_out, not_1_out);
  and and_25 (LSB_5, in_9, 1'b1);
  and and_26 (out_71, LSB, 1'b1);
  and and_27 (out_72, in_11, 1'b1);
  and and_28 (out_73, in_12, 1'b1);
  and and_29 (out_74, ALU_output, 1'b1);
  and and_30 (MSB_5, in_15, 1'b1);
  and and_31 (out_75, in_14, 1'b1);
  and and_32 (and_32_out, in_12, in_9);
  and and_33 (and_32_out, and_10_out, Read);
  and and_34 (and_34_out, and_10_out, in_27);
  and and_35 (and_35_out, and_10_out, in_26);
  and and_36 (and_36_out, and_10_out, in_25);
  and and_37 (LSB_4, Read, and_9_out);
  and and_38 (out_46, in_27, and_9_out);
  and and_39 (out_47, in_26, and_9_out);
  and and_40 (MSB_4, in_25, and_9_out);
  and and_41 (out_77, MSB, 1'b1);
  and and_42 (and_35_out, in_12, in_11);
  and and_43 (and_34_out, in_12, LSB);
  and and_44 (and_36_out, in_12, in_12);
  and and_45 (LSB_3, and_32_out, not_5_out);
  not not_5 (not_5_out, and_13_out);
  and and_46 (out_40, and_34_out, not_6_out);
  not not_6 (not_6_out, and_13_out);
  and and_47 (out_41, and_35_out, not_7_out);
  not not_7 (not_7_out, and_13_out);
  and and_48 (MSB_3, and_36_out, not_8_out);
  not not_8 (not_8_out, and_13_out);

  assign Compare = LSB;
  assign Counter_Enable = in_29;
  assign out_57 = A_B;
  assign out_58 = A_B_2;
  assign out_59 = A_B_3;
  assign out_61 = in_8;
  assign out_62 = in_7;
  assign out_63 = in_6;
  assign out_64 = in_5;
  assign out_65 = in_1;
  assign out_66 = in_2;
  assign out_67 = in_3;
  assign out_68 = Address_Line;
  assign out_69 = in_29;
  assign out_78 = ERROR;
  assign Read_2 = 1'b1;

  // Notes on the sheet:
  //   They'll need regsiters too :(
  //   3 separate address jumps
  //   Program Counter Input
  //   Address Input
  //   Insert Counter New Address
  //   Jump Address
  //   Program Counter Address Output
  //   Instruction Line
  //   ROM Registers
  //   Instruction Register
  //   Instruction Output
  //   Computer On/Off switch
  //   Control Unit
  //   Push Accumulator Value out to ALU
  //   OUTPUT
  //   Accumulator Value going back to ALU
  //   ALU unit input A
  //   ALU unit input B
  //   Operand
  //   Accumulative Register
  //   ADd A and B registers
endmodule
