// Logisim project Program Counter.circ as structural Verilog: 1 circuit, main circuit main
module main (
  input  Clear_Counter,
  input  Enable_Counter,
  input  in_3,
  input  in_4,
  input  in_5,
  input  in_6,
  input  in_7,
  input  in_8,
  input  in_9,
  input  in_10,
  input  in_11,
  output out_12,
  output out_13,
  output out_14,
  output out_15,
  output out_16,
  output out_17,
  output out_18,
  output out_19,
  output out_20
);

  wire and_1_out, and_2_out, and_3_out, and_4_out, and_5_out, and_6_out, and_7_out, and_8_out, and_9_out,
       and_10_out, and_11_out, and_12_out, and_13_out, and_14_out, and_15_out, clock_1_out;

  Clock clock_1 (.out(clock_1_out));
  and and_1 (and_1_out, Enable_Counter, out_12);
  and and_2 (and_2_out, in_3, in_4);
  and and_3 (and_3_out, in_3, in_5);
  and and_4 (and_4_out, in_3, in_6);
  and and_5 (and_5_out, in_3, in_7);
  and and_6 (and_6_out, in_3, in_8);
  and and_7 (and_7_out, in_3, in_9);
  and and_8 (and_8_out, in_3, in_10);
  and and_9 (and_9_out, in_3, in_11);
  J_K_Flip_Flop #(.trigger("falling")) j_k_ff_1 (
    .J(Enable_Counter), .clk(clock_1_out), .K(Enable_Counter), .Q(out_12), .preset(and_2_out),
    .reset(Clear_Counter));  // open: Qn, en
  and and_10 (and_10_out, and_1_out, out_13);
  J_K_Flip_Flop #(.trigger("falling")) j_k_ff_2 (
    .J(and_1_out), .clk(clock_1_out), .K(and_1_out), .Q(out_13), .preset(and_3_out), .reset(Clear_Counter));  // open: Qn, en
  and and_11 (and_11_out, and_10_out, out_14);
  J_K_Flip_Flop #(.trigger("falling")) j_k_ff_3 (
    .J(and_10_out), .clk(clock_1_out), .K(and_10_out), .Q(out_14), .preset(and_4_out), .reset(Clear_Counter));  // open: Qn, en
  and and_12 (and_12_out, and_11_out, out_15);
  J_K_Flip_Flop #(.trigger("falling")) j_k_ff_4 (
    .J(and_11_out), .clk(clock_1_out), .K(and_11_out), .Q(out_15), .preset(and_5_out), .reset(Clear_Counter));  // open: Qn, en
  and and_13 (and_13_out, and_12_out, out_16);
  J_K_Flip_Flop #(.trigger("falling")) j_k_ff_5 (
    .J(and_12_out), .clk(clock_1_out), .K(and_12_out), .Q(out_16), .preset(and_6_out), .reset(Clear_Counter));  // open: Qn, en
  and and_14 (and_14_out, and_13_out, out_17);
  J_K_Flip_Flop #(.trigger("falling")) j_k_ff_6 (
    .J(and_13_out), .clk(clock_1_out), .K(and_13_out), .Q(out_17), .preset(and_7_out), .reset(Clear_Counter));  // open: Qn, en
  and and_15 (and_15_out, and_14_out, out_18);
  J_K_Flip_Flop #(.trigger("falling")) j_k_ff_7 (
    .J(and_14_out), .clk(clock_1_out), .K(and_14_out), .Q(out_18), .preset(and_8_out), .reset(Clear_Counter));  // open: Qn, en
  and and_16 (out_20, and_15_out, out_19);
  J_K_Flip_Flop #(.trigger("falling")) j_k_ff_8 (
    .J(and_15_out), .clk(clock_1_out), .K(and_15_out), .Q(out_19), .preset(and_9_out), .reset(Clear_Counter));  // open: Qn, en

  // Notes on the sheet:
  //   Send Instruction
  //   Manual Address input
  //   Program Counter
  //   Missing an incrementer
endmodule
