// Logisim project RAM types.circ as structural Verilog: 1 circuit, main circuit main
module main (
  input  in_1,
  input  in_2,
  input  B3,
  input  B2,
  input  in_5,
  input  B0,
  input  in_7,
  input  A0,
  input  in_9,
  input  in_10,
  input  in_11,
  input  A1,
  input  B0_2,
  input  B1,
  input  in_15,
  input  B2_2,
  input  B3_2,
  input  A2,
  input  A0_2,
  input  A1_2,
  input  B0_3,
  input  A2_2,
  input  Load,
  input  A0_3,
  input  A3,
  input  Read,
  input  Address,
  input  A3_2,
  input  B1_2,
  input  Clear,
  input  A1_3,
  input  in_32,
  input  in_33,
  input  B2_3,
  input  in_35,
  input  A2_3,
  input  in_37,
  input  B3_3,
  input  A3_3,
  input  in_40,
  input  B0_4,
  input  in_42,
  input  in_43,
  input  in_44,
  input  in_45,
  input  Clear_2,
  input  in_47,
  input  in_48,
  input  in_49,
  input  A0_4,
  input  in_51,
  input  B1_3,
  input  A1_4,
  input  B2_4,
  input  A2_4,
  input  B3_4,
  input  A3_4,
  input  in_58,
  input  B0_5,
  input  A0_5,
  input  B1_4,
  input  A1_5,
  input  Divide_Button,
  input  B2_5,
  input  A3_5,
  input  A2_5,
  input  A2_6,
  input  A1_6,
  input  A0_6,
  input  B3_5,
  input  B2_6,
  input  B3_6,
  input  B1_5,
  input  A3_6,
  input  B0_6,
  input  _1,
  input  in_77,
  input  in_78,
  input  in_79,
  input  in_80,
  input  _0,
  input  in_82,
  input  in_83,
  input  in_84,
  input  B0_7,
  input  A0_7,
  input  B1_6,
  input  A1_7,
  input  B2_7,
  input  A2_7,
  input  B3_7,
  input  A3_7,
  output out_93,
  output out_94,
  output out_95,
  output out_96,
  output out_97,
  output out_98,
  output out_99,
  output out_100,
  output out_101,
  output out_102,
  output out_103,
  output out_104,
  output out_105,
  output out_106,
  output out_107,
  output out_108,
  output Not_B,
  output out_110,
  output out_111,
  output And,
  output out_113,
  output out_114,
  output out_115,
  output out_116,
  output out_117,
  output out_118,
  output out_119,
  output A_B,
  output ERROR,
  output A_B_2
);

  wire and_1_out, and_2_out, and_3_out, and_4_out, and_5_out, and_6_out, and_7_out, and_8_out, and_9_out,
       and_11_out, and_12_out, and_13_out, and_14_out, and_15_out, and_16_out, and_17_out, and_18_out,
       and_19_out, and_20_out, and_21_out, and_22_out, and_23_out, and_24_out, and_25_out, and_26_out,
       and_27_out, and_28_out, and_29_out, and_30_out, and_31_out, and_32_out, and_33_out, and_34_out,
       and_35_out, and_36_out, and_37_out, and_38_out, and_39_out, and_40_out, and_41_out, and_42_out,
       and_44_out, and_45_out, and_46_out, and_47_out, and_48_out, and_51_out, and_52_out, and_53_out,
       and_54_out, and_55_out, and_56_out, and_58_out, and_60_out, and_61_out, and_62_out, and_63_out,
       and_64_out, and_65_out, and_66_out, and_67_out, and_68_out, and_69_out, and_70_out, and_71_out,
       and_72_out, and_73_out, and_74_out, and_75_out, and_76_out, and_77_out, and_78_out, and_79_out,
       and_80_out, and_81_out, and_82_out, and_83_out, and_84_out, and_86_out, and_87_out, and_88_out,
       and_89_out, and_90_out, and_91_out, and_92_out, and_93_out, and_94_out, and_95_out, and_96_out,
       and_97_out, and_99_out, and_100_out, and_101_out, and_102_out, and_103_out, and_104_out, and_105_out,
       and_106_out, and_107_out, and_108_out, and_109_out, and_110_out, and_111_out, and_112_out,
       and_113_out, and_122_out, and_123_out, and_124_out, and_125_out, and_126_out, and_127_out,
       and_128_out, and_129_out, and_130_out, and_131_out, and_132_out, and_133_out, and_134_out,
       and_135_out, and_136_out, and_137_out, and_138_out, and_139_out, and_140_out, and_141_out,
       and_142_out, and_143_out, and_144_out, and_145_out, and_146_out, buffer_1_out, clock_1_out,
       clock_2_out, clock_3_out, d_ff_1_q, j_k_ff_1_q, j_k_ff_2_q, j_k_ff_3_q, j_k_ff_4_q, nand_1_out,
       nand_2_out, nand_3_out, nor_1_out, nor_2_out, nor_3_out, nor_4_out, not_1_out, not_2_out, not_3_out,
       not_4_out, not_5_out, not_6_out, not_7_out, not_8_out, not_9_out, not_10_out, not_11_out, not_12_out,
       not_13_out, not_14_out, not_15_out, not_16_out, not_17_out, not_18_out, not_19_out, not_20_out,
       not_21_out, not_22_out, or_1_out, or_2_out, or_3_out, or_4_out, or_5_out, or_6_out, or_7_out,
       or_8_out, or_9_out, or_10_out, or_13_out, or_14_out, or_15_out, or_16_out, or_19_out, or_20_out,
       or_21_out, or_22_out, or_23_out, or_24_out, or_25_out, or_26_out, or_27_out, or_28_out, or_29_out,
       or_30_out, or_31_out, or_32_out, or_33_out, or_34_out, or_35_out, or_36_out, undriven, undriven_2,
       undriven_3, undriven_4, undriven_5, undriven_6, undriven_7, undriven_8, undriven_9, undriven_10,
       xor_1_out, xor_2_out, xor_3_out, xor_4_out, xor_5_out, xor_6_out, xor_7_out, xor_8_out, xor_9_out,
       xor_10_out, xor_11_out, xor_12_out, xor_13_out, xor_14_out, xor_15_out, xor_16_out, xor_17_out,
       xor_18_out, xor_19_out, xor_21_out, xor_23_out, xor_24_out, xor_26_out, xor_27_out, xor_28_out,
       xor_29_out, xor_30_out, xor_31_out, xor_32_out, xor_33_out, xor_36_out, xor_37_out, xor_38_out,
       xor_39_out, xor_40_out, xor_41_out, xor_42_out, xor_43_out, xor_44_out, xor_45_out, xor_46_out,
       xor_47_out, xor_48_out, xor_49_out, xor_50_out, xor_51_out, xor_52_out, xor_53_out, xor_55_out,
       xor_56_out, xor_57_out, xor_58_out, xor_59_out, xor_60_out, xor_61_out, xor_62_out, xor_63_out,
       xor_64_out, xor_65_out, xor_66_out, xor_67_out, xor_69_out, xor_70_out, xor_71_out, xor_72_out,
       xor_73_out;

  Clock clock_1 (.out(clock_1_out));
  and and_1 (and_1_out, Read, Address);
  and and_2 (and_2_out, Address, Clear);
  and and_3 (and_3_out, in_32, in_33);
  J_K_Flip_Flop j_k_ff_1 (.J(in_2), .clk(clock_1_out), .K(in_2), .Q(j_k_ff_1_q));  // open: Qn, preset, en, reset
  and and_4 (and_4_out, or_1_out, in_2);
  and and_5 (and_5_out, in_11, buffer_1_out);
  buf buffer_1 (buffer_1_out, in_15);
  and and_6 (and_6_out, or_2_out, not_1_out);
  not not_1 (not_1_out, in_15);
  not not_2 (not_2_out, and_2_out);
  xor xor_1 (xor_1_out, in_32, in_33);
  or or_1 (or_1_out, j_k_ff_1_q, in_7);
  or or_2 (or_2_out, and_5_out, and_6_out);
  nand nand_1 (nand_1_out, not_2_out, Load);
  nand nand_2 (nand_2_out, nand_1_out, nand_3_out);
  nand nand_3 (nand_3_out, not_2_out, d_ff_1_q);
  xor xor_2 (xor_2_out, xor_1_out, in_37);
  and and_7 (and_7_out, in_37, xor_1_out);
  J_K_Flip_Flop j_k_ff_2 (
    .J(and_4_out), .clk(clock_1_out), .K(and_4_out), .Q(j_k_ff_2_q));  // open: Qn, preset, en, reset
  and and_8 (and_8_out, j_k_ff_2_q, and_4_out);
  assign out_98 = in_9 ? or_2_out : 1'bz;  // Controlled_Buffer controlled_buffer_1
  Clock clock_2 (.out(clock_2_out));
  D_Flip_Flop d_ff_1 (.clk(clock_2_out), .D(nand_2_out), .Q(d_ff_1_q));  // open: Qn, preset, en, reset
  or or_3 (or_3_out, and_7_out, and_3_out);
  and and_9 (and_9_out, j_k_ff_3_q, and_8_out);
  assign out_102 = and_1_out ? d_ff_1_q : 1'bz;  // Controlled_Buffer controlled_buffer_2
  J_K_Flip_Flop j_k_ff_3 (
    .J(and_8_out), .clk(clock_1_out), .K(and_8_out), .Q(j_k_ff_3_q));  // open: Qn, preset, en, reset
  J_K_Flip_Flop j_k_ff_4 (
    .J(and_9_out), .clk(clock_1_out), .K(and_9_out), .Q(j_k_ff_4_q));  // open: Qn, preset, en, reset
  and and_10 (out_97, j_k_ff_4_q, and_9_out);
  not not_3 (not_3_out, B0_4);
  not not_4 (not_4_out, B1_3);
  not not_5 (not_5_out, B2_4);
  not not_6 (not_6_out, B3_4);
  Clock clock_3 (.out(clock_3_out));
  xor xor_3 (xor_3_out, B0_3, A0_3);
  and and_11 (and_11_out, A0_3, B0_3);
  xor xor_4 (xor_4_out, B1_2, A1_3);
  and and_12 (and_12_out, B1_2, A1_3);
  xor xor_5 (xor_5_out, B2_3, A2_3);
  and and_13 (and_13_out, B2_3, A2_3);
  xor xor_6 (xor_6_out, B3_3, A3_3);
  and and_14 (and_14_out, B3_3, A3_3);
  xor xor_7 (xor_7_out, not_3_out, A0_4);
  and and_15 (and_15_out, not_3_out, A0_4);
  xor xor_8 (xor_8_out, not_4_out, A1_4);
  and and_16 (and_16_out, not_4_out, A1_4);
  xor xor_9 (xor_9_out, not_5_out, A2_4);
  and and_17 (and_17_out, not_5_out, A2_4);
  xor xor_10 (xor_10_out, not_6_out, A3_4);
  and and_18 (and_18_out, not_6_out, A3_4);
  J_K_Flip_Flop j_k_ff_5 (.J(in_1), .clk(clock_3_out), .K(in_1), .Qn(out_93));  // open: Q, preset, en, reset
  xor xor_11 (xor_11_out, xor_4_out, and_11_out);
  and and_19 (and_19_out, and_11_out, xor_4_out);
  xor xor_12 (xor_12_out, xor_5_out, or_4_out);
  and and_20 (and_20_out, or_4_out, xor_5_out);
  xor xor_13 (xor_13_out, xor_6_out, or_5_out);
  and and_21 (and_21_out, or_5_out, xor_6_out);
  xor xor_14 (xor_14_out, xor_7_out, in_40);
  and and_22 (and_22_out, in_40, xor_7_out);
  xor xor_15 (xor_15_out, xor_8_out, or_7_out);
  and and_23 (and_23_out, or_7_out, xor_8_out);
  xor xor_16 (xor_16_out, xor_9_out, or_8_out);
  and and_24 (and_24_out, or_8_out, xor_9_out);
  xor xor_17 (xor_17_out, xor_10_out, or_9_out);
  and and_25 (and_25_out, or_9_out, xor_10_out);
  J_K_Flip_Flop j_k_ff_6 (.J(in_1), .clk(out_93), .K(in_1), .Qn(out_94));  // open: Q, preset, en, reset
  or or_4 (or_4_out, and_19_out, and_12_out);
  or or_5 (or_5_out, and_20_out, and_13_out);
  or or_6 (or_6_out, and_21_out, and_14_out);
  or or_7 (or_7_out, and_22_out, and_15_out);
  or or_8 (or_8_out, and_23_out, and_16_out);
  or or_9 (or_9_out, and_24_out, and_17_out);
  or or_10 (or_10_out, and_25_out, and_18_out);
  J_K_Flip_Flop j_k_ff_7 (.J(in_1), .clk(out_94), .K(in_1), .Qn(out_95));  // open: Q, preset, en, reset
  xor xor_18 (xor_18_out, or_9_out, or_10_out);
  J_K_Flip_Flop j_k_ff_8 (.J(in_1), .clk(out_95), .K(in_1), .Qn(out_96));  // open: Q, preset, en, reset
  and and_26 (and_26_out, undriven_2, undriven_3);
  and and_27 (and_27_out, xor_19_out, undriven);
  // OR_Gate or_11 has open pins: in0=and_26_out, in1=and_27_out, out=open
  xor xor_19 (xor_19_out, undriven_2, undriven_3);
  // XOR_Gate xor_20 has open pins: in0=undriven, in1=xor_19_out, out=open
  and and_28 (and_28_out, undriven_5, undriven_6);
  and and_29 (and_29_out, xor_21_out, undriven_4);
  xor xor_21 (xor_21_out, undriven_5, undriven_6);
  // XOR_Gate xor_22 has open pins: in0=undriven_4, in1=xor_21_out, out=open
  // OR_Gate or_12 has open pins: in0=and_28_out, in1=and_29_out, out=open
  and and_30 (and_30_out, or_13_out, or_14_out);
  xor xor_23 (xor_23_out, or_13_out, or_14_out);
  and and_31 (and_31_out, undriven_8, undriven_10);
  and and_32 (and_32_out, xor_26_out, and_40_out);
  or or_13 (or_13_out, and_31_out, and_32_out);
  and and_33 (and_33_out, undriven_7, undriven_9);
  and and_34 (and_34_out, xor_28_out, and_41_out);
  xor xor_24 (xor_24_out, and_41_out, xor_28_out);
  or or_14 (or_14_out, and_33_out, and_34_out);
  and and_35 (and_35_out, xor_24_out, xor_27_out);
  and and_36 (and_36_out, xor_29_out, xor_23_out);
  xor xor_25 (out_115, xor_23_out, xor_29_out);
  or or_15 (or_15_out, and_35_out, and_36_out);
  xor xor_26 (xor_26_out, undriven_8, undriven_10);
  xor xor_27 (xor_27_out, and_40_out, xor_26_out);
  xor xor_28 (xor_28_out, undriven_7, undriven_9);
  xor xor_29 (xor_29_out, xor_24_out, xor_27_out);
  and and_37 (and_37_out, and_54_out, and_52_out);
  and and_38 (and_38_out, xor_32_out, and_42_out);
  or or_16 (or_16_out, and_37_out, and_38_out);
  and and_39 (and_39_out, and_55_out, xor_33_out);
  xor xor_30 (xor_30_out, and_55_out, xor_33_out);
  and and_40 (and_40_out, or_16_out, and_39_out);
  xor xor_31 (xor_31_out, or_16_out, and_39_out);
  and and_41 (and_41_out, xor_31_out, xor_30_out);
  and and_42 (and_42_out, and_53_out, and_54_out);
  xor xor_32 (xor_32_out, and_54_out, and_52_out);
  xor xor_33 (xor_33_out, and_42_out, xor_32_out);
  xor xor_34 (out_111, xor_30_out, xor_31_out);
  // AND_Gate and_43 has open pins: in0=A3_2, in1=B3, out=open
  xor xor_35 (out_106, and_53_out, and_54_out);
  and and_44 (and_44_out, A0, B3);
  and and_45 (and_45_out, A1, B3);
  and and_46 (and_46_out, A1, B2);
  and and_47 (and_47_out, A2, B3);
  and and_48 (and_48_out, A2, B2);
  // AND_Gate and_49 has open pins: in0=A3_2, in1=in_5, out=open
  // AND_Gate and_50 has open pins: in0=A3_2, in1=B2, out=open
  and and_51 (and_51_out, A0, in_5);
  and and_52 (and_52_out, A0, B2);
  and and_53 (and_53_out, A1, B0);
  and and_54 (and_54_out, A1, in_5);
  and and_55 (and_55_out, A2, B0);
  and and_56 (and_56_out, A2, in_5);
  // AND_Gate and_57 has open pins: in0=A3_2, in1=B0, out=open
  and and_58 (and_58_out, A0_6, Divide_Button);
  and and_59 (out_107, A0, B0);
  and and_60 (and_60_out, A2_6, Divide_Button);
  and and_61 (and_61_out, A1_6, Divide_Button);
  and and_62 (and_62_out, B1_5, Divide_Button);
  and and_63 (and_63_out, B0_6, Divide_Button);
  and and_64 (and_64_out, A3_5, Divide_Button);
  and and_65 (and_65_out, B3_5, Divide_Button);
  buf and_66 (and_66_out, B2_6);  // AND_Gate
  not not_7 (not_7_out, and_64_out);
  not not_8 (not_8_out, and_65_out);
  not not_9 (not_9_out, and_60_out);
  not not_10 (not_10_out, and_66_out);
  not not_11 (not_11_out, and_61_out);
  not not_12 (not_12_out, and_62_out);
  not not_13 (not_13_out, and_58_out);
  not not_14 (not_14_out, and_63_out);
  and and_67 (and_67_out, not_7_out, and_65_out);
  and and_68 (and_68_out, and_64_out, not_8_out);
  and and_69 (and_69_out, not_9_out, and_66_out);
  and and_70 (and_70_out, and_60_out, not_10_out);
  and and_71 (and_71_out, not_11_out, and_62_out);
  and and_72 (and_72_out, and_61_out, not_12_out);
  and and_73 (and_73_out, not_13_out, and_63_out);
  and and_74 (and_74_out, and_58_out, not_14_out);
  nor nor_1 (nor_1_out, and_67_out, and_68_out);
  nor nor_2 (nor_2_out, and_69_out, and_70_out);
  nor nor_3 (nor_3_out, and_71_out, and_72_out);
  nor nor_4 (nor_4_out, and_73_out, and_74_out);
  not not_15 (not_15_out, B0_7);
  not not_16 (not_16_out, B1_6);
  not not_17 (not_17_out, B2_7);
  not not_18 (not_18_out, B3_7);
  xor xor_36 (xor_36_out, not_15_out, A0_7);
  and and_75 (and_75_out, not_15_out, A0_7);
  xor xor_37 (xor_37_out, not_16_out, A1_7);
  and and_76 (and_76_out, not_16_out, A1_7);
  xor xor_38 (xor_38_out, not_17_out, A2_7);
  and and_77 (and_77_out, not_17_out, A2_7);
  xor xor_39 (xor_39_out, not_18_out, A3_7);
  and and_78 (and_78_out, not_18_out, A3_7);
  not not_19 (not_19_out, B0_5);
  not not_20 (not_20_out, B1_4);
  not not_21 (not_21_out, B2_5);
  not not_22 (not_22_out, B3_6);
  and and_79 (and_79_out, nor_1_out, and_69_out);
  and and_80 (and_80_out, nor_1_out, and_70_out);
  and and_81 (and_81_out, nor_1_out, nor_2_out, and_71_out);
  and and_82 (and_82_out, nor_1_out, nor_2_out, and_72_out);
  and and_83 (and_83_out, nor_1_out, nor_2_out, nor_3_out, and_73_out);
  and and_84 (and_84_out, nor_1_out, nor_2_out, nor_3_out, and_74_out);
  and and_85 (A_B_2, nor_1_out, nor_2_out, nor_3_out, nor_4_out);
  xor xor_40 (xor_40_out, xor_37_out, or_20_out);
  and and_86 (and_86_out, or_20_out, xor_37_out);
  and and_87 (and_87_out, not_20_out, A1_5);
  or or_17 (ERROR, and_67_out, and_81_out, and_83_out, and_79_out);
  or or_18 (A_B, and_68_out, and_80_out, and_82_out, and_84_out);
  xor xor_41 (xor_41_out, xor_36_out, in_84);
  and and_88 (and_88_out, in_84, xor_36_out);
  or or_19 (or_19_out, and_86_out, and_76_out);
  xor xor_42 (xor_42_out, xor_38_out, or_19_out);
  and and_89 (and_89_out, or_19_out, xor_38_out);
  xor xor_43 (xor_43_out, xor_39_out, or_21_out);
  and and_90 (and_90_out, or_21_out, xor_39_out);
  xor xor_44 (xor_44_out, not_19_out, A0_5);
  and and_91 (and_91_out, not_19_out, A0_5);
  xor xor_45 (xor_45_out, not_20_out, A1_5);
  xor xor_46 (xor_46_out, not_21_out, A2_5);
  and and_92 (and_92_out, not_21_out, A2_5);
  xor xor_47 (xor_47_out, not_22_out, A3_6);
  and and_93 (and_93_out, not_22_out, A3_6);
  or or_20 (or_20_out, and_88_out, and_75_out);
  or or_21 (or_21_out, and_89_out, and_77_out);
  or or_22 (or_22_out, and_90_out, and_78_out);
  xor xor_48 (xor_48_out, xor_44_out, in_58);
  and and_94 (and_94_out, in_58, xor_44_out);
  xor xor_49 (xor_49_out, xor_45_out, or_23_out);
  and and_95 (and_95_out, or_23_out, xor_45_out);
  xor xor_50 (xor_50_out, xor_46_out, or_24_out);
  and and_96 (and_96_out, or_24_out, xor_46_out);
  xor xor_51 (xor_51_out, xor_47_out, or_25_out);
  and and_97 (and_97_out, or_25_out, xor_47_out);
  xor xor_52 (xor_52_out, or_21_out, or_22_out);
  or or_23 (or_23_out, and_94_out, and_91_out);
  or or_24 (or_24_out, and_95_out, and_87_out);
  or or_25 (or_25_out, and_96_out, and_92_out);
  or or_26 (or_26_out, and_97_out, and_93_out);
  xor xor_53 (xor_53_out, or_25_out, or_26_out);
  and and_98 (out_99, A0_2, B0_2);
  and and_99 (and_99_out, A0_2, B1);
  and and_100 (and_100_out, A0_2, B2_2);
  and and_101 (and_101_out, A0_2, B3_2);
  and and_102 (and_102_out, A1_2, B0_2);
  and and_103 (and_103_out, A1_2, B1);
  and and_104 (and_104_out, A1_2, B2_2);
  and and_105 (and_105_out, A1_2, B3_2);
  and and_106 (and_106_out, A2_2, B0_2);
  and and_107 (and_107_out, A2_2, B1);
  and and_108 (and_108_out, A2_2, B2_2);
  and and_109 (and_109_out, A2_2, B3_2);
  and and_110 (and_110_out, A3, B0_2);
  and and_111 (and_111_out, A3, B1);
  and and_112 (and_112_out, A3, B2_2);
  and and_113 (and_113_out, A3, B3_2);
  and and_114 (out_116, _1, A_B_2);
  and and_115 (out_117, in_77, A_B_2);
  and and_116 (out_118, in_78, A_B_2);
  and and_117 (out_119, in_79, A_B_2);
  // AND_Gate and_118 is placed but not wired
  // AND_Gate and_119 is placed but not wired
  // AND_Gate and_120 is placed but not wired
  // AND_Gate and_121 is placed but not wired
  xor xor_54 (out_100, and_102_out, and_99_out);
  and and_122 (and_122_out, and_99_out, and_102_out);
  xor xor_55 (xor_55_out, and_103_out, and_100_out);
  and and_123 (and_123_out, and_103_out, and_100_out);
  xor xor_56 (xor_56_out, and_104_out, and_101_out);
  and and_124 (and_124_out, and_104_out, and_101_out);
  xor xor_57 (xor_57_out, and_105_out, in_10);
  and and_125 (and_125_out, and_105_out, in_10);
  xor xor_58 (xor_58_out, and_110_out, and_107_out);
  and and_126 (and_126_out, and_107_out, and_110_out);
  xor xor_59 (xor_59_out, and_111_out, and_108_out);
  and and_127 (and_127_out, and_111_out, and_108_out);
  xor xor_60 (xor_60_out, and_112_out, and_109_out);
  and and_128 (and_128_out, and_112_out, and_109_out);
  xor xor_61 (xor_61_out, and_113_out, in_10);
  and and_129 (and_129_out, and_113_out, in_10);
  xor xor_62 (xor_62_out, xor_55_out, and_122_out);
  and and_130 (and_130_out, and_122_out, xor_55_out);
  xor xor_63 (xor_63_out, xor_56_out, or_27_out);
  and and_131 (and_131_out, or_27_out, xor_56_out);
  xor xor_64 (xor_64_out, xor_57_out, or_28_out);
  and and_132 (and_132_out, or_28_out, xor_57_out);
  xor xor_65 (xor_65_out, xor_59_out, and_126_out);
  and and_133 (and_133_out, and_126_out, xor_59_out);
  xor xor_66 (xor_66_out, xor_60_out, or_30_out);
  and and_134 (and_134_out, or_30_out, xor_60_out);
  xor xor_67 (xor_67_out, xor_61_out, or_31_out);
  and and_135 (and_135_out, or_31_out, xor_61_out);
  or or_27 (or_27_out, and_130_out, and_123_out);
  or or_28 (or_28_out, and_131_out, and_124_out);
  or or_29 (or_29_out, and_132_out, and_125_out);
  or or_30 (or_30_out, and_133_out, and_127_out);
  or or_31 (or_31_out, and_134_out, and_128_out);
  or or_32 (or_32_out, and_135_out, and_129_out);
  xor xor_68 (out_101, xor_62_out, and_106_out);
  and and_136 (and_136_out, and_106_out, xor_62_out);
  xor xor_69 (xor_69_out, xor_63_out, xor_58_out);
  and and_137 (and_137_out, xor_63_out, xor_58_out);
  xor xor_70 (xor_70_out, xor_64_out, xor_65_out);
  and and_138 (and_138_out, xor_64_out, xor_65_out);
  xor xor_71 (xor_71_out, or_29_out, xor_66_out);
  and and_139 (and_139_out, or_29_out, xor_66_out);
  xor xor_72 (xor_72_out, in_10, xor_67_out);
  and and_140 (and_140_out, in_10, xor_67_out);
  xor xor_73 (xor_73_out, in_10, or_32_out);
  and and_141 (and_141_out, in_10, or_32_out);
  xor xor_74 (out_103, xor_69_out, and_136_out);
  and and_142 (and_142_out, and_136_out, xor_69_out);
  xor xor_75 (out_104, xor_70_out, or_33_out);
  and and_143 (and_143_out, or_33_out, xor_70_out);
  xor xor_76 (out_105, xor_71_out, or_34_out);
  and and_144 (and_144_out, or_34_out, xor_71_out);
  xor xor_77 (out_108, xor_72_out, or_35_out);
  and and_145 (and_145_out, or_35_out, xor_72_out);
  xor xor_78 (out_113, xor_73_out, or_36_out);
  and and_146 (and_146_out, or_36_out, xor_73_out);
  or or_33 (or_33_out, and_142_out, and_137_out);
  or or_34 (or_34_out, and_143_out, and_138_out);
  or or_35 (or_35_out, and_144_out, and_139_out);
  or or_36 (or_36_out, and_145_out, and_140_out);
  or or_37 (out_114, and_146_out, and_141_out);
  // NOT_Gate not_23 is placed but not wired

  // Notes on the sheet:
  //   Send Instruction and Inputs
  //   Pick Instruction
  //   Input A
  //   Input B
  //   Outputs
  //   Missing some features
  //   Read/ Output Line
  //   Input Value Line
  //   Write/ Erase Line
  //   Address Line
  //   Full Adder
  //   Manual Instruction Insertion
  //   I/O port
  //   1 bit of sketchy RAM
  //   1 bit synchronized non-sketchy RAM
  //   Input A
  //   Clear
  //   Counter
  //   Overflow Flag
  //   Need to have an increment by 1 for the program counter and also for the adder and subtractor (i.e the carry in)
  //   B1
  //   A<B
endmodule
